// Logisim project MAIN_CIRCUIT.circ as structural Verilog: 5 circuits, main circuit main
module main (
  input  [3:0] A,
  input  [3:0] B,
  input  CS2,
  input  CS1,
  input  CS0,
  output [3:0] out_6,
  output out_7,
  output C,
  output V,
  output Z,
  output S
);

  wire designing_4_bit_x_y_with_z_1_x0, designing_4_bit_x_y_with_z_1_x1, designing_4_bit_x_y_with_z_1_x2,
       designing_4_bit_x_y_with_z_1_x3, designing_4_bit_x_y_with_z_1_y0, designing_4_bit_x_y_with_z_1_y1,
       designing_4_bit_x_y_with_z_1_y2, designing_4_bit_x_y_with_z_1_y3, designing_4_bit_x_y_with_z_1_z;

  DESIGNING_4_BIT_X_Y_WITH_Z designing_4_bit_x_y_with_z_1 (
    .CS2(CS2), .CS1(CS1), .CS0(CS0), .X3(designing_4_bit_x_y_with_z_1_x3),
    .X2(designing_4_bit_x_y_with_z_1_x2), .X1(designing_4_bit_x_y_with_z_1_x1),
    .X0(designing_4_bit_x_y_with_z_1_x0), .A(A), .B(B), .Y3(designing_4_bit_x_y_with_z_1_y3),
    .Y2(designing_4_bit_x_y_with_z_1_y2), .Y1(designing_4_bit_x_y_with_z_1_y1),
    .Y0(designing_4_bit_x_y_with_z_1_y0), .Z(designing_4_bit_x_y_with_z_1_z));
  _7483 u_7483_1 (
    ._1__A4(designing_4_bit_x_y_with_z_1_x3), ._2__S3(out_6[2]), ._3__A3(designing_4_bit_x_y_with_z_1_x2),
    ._4__B3(designing_4_bit_x_y_with_z_1_y2), ._5__Vcc(1'b1), ._6__S2(out_6[1]),
    ._7__B2(designing_4_bit_x_y_with_z_1_y1), ._8__A2(designing_4_bit_x_y_with_z_1_x1),
    ._16__B4(designing_4_bit_x_y_with_z_1_y3), ._15__S4(out_6[3]), ._14_Cout(out_7),
    ._13__Cin(designing_4_bit_x_y_with_z_1_z), ._12__GND(1'b0), ._11__B1(designing_4_bit_x_y_with_z_1_y0),
    ._10__A1(designing_4_bit_x_y_with_z_1_x0), ._9__S1(out_6[0]));
  Flag flag_1 (
    .in_4(out_6), .A4(designing_4_bit_x_y_with_z_1_x3), .B4(designing_4_bit_x_y_with_z_1_y3), .Cout(out_7),
    .C(C), .V(V), .Z(Z), .S(S));
endmodule

module DETERMINATION_OF_X (
  input  CS2,
  input  CS1,
  input  CS0,
  input  A,
  input  B,
  output X
);

  wire n7404_1__2__1y, n7408_1__3__1y, n7432_1__3__1y, n7486_1__3__1y, n7486_1__6__2y;

  _7408 u_7408_1 (
    ._1__1A(B), ._2__1B(CS2), ._3__1Y(n7408_1__3__1y), ._7__GND(1'b0), ._14__Vcc(1'b1));  // open: _4__2A, _5__2B, _6__2Y, _13__4B, _12__4A, _11__4Y, _10__3B, _9__3A, _8__3Y
  _7404 u_7404_1 (
    ._1__1A(n7486_1__6__2y), ._2__1Y(n7404_1__2__1y), ._7__GND(1'b0), ._14__Vcc(1'b1));  // open: _3__2A, _4__2Y, _5__3A, _6__3Y, _13__6A, _12__6Y, _11__5A, _10__5Y, _9__4A, _8__4Y
  _7432 u_7432_1 (
    ._1__1A(A), ._2__1B(n7408_1__3__1y), ._3__1Y(n7432_1__3__1y), ._7__GND(1'b0), ._14__Vcc(1'b1));  // open: _4__2A, _5__2B, _6__2Y, _13__4B, _12__4A, _11__4Y, _10__3B, _9__3A, _8__3Y
  _74153 u_74153_1 (
    ._1__nG1(1'b0), ._2__B(CS1), ._3__1C3(n7404_1__2__1y), ._4__1C2(n7486_1__3__1y),
    ._5__1C1(n7432_1__3__1y), ._6__1C0(A), ._7__Y1(X), ._8__GND(1'b0), ._16__Vcc(1'b1), ._14__A(CS0));  // open: _15__nG2, _13__2C3, _12__2C2, _11__2C1, _10__2C0, _9__Y2
  _7486 u_7486_1 (
    ._1__1A(B), ._2__1B(A), ._3__1Y(n7486_1__3__1y), ._4__2A(A), ._5__2B(CS2), ._6__2Y(n7486_1__6__2y),
    ._7__GND(1'b0), ._14__Vcc(1'b1));  // open: _13__4B, _12__4A, _11__4Y, _10__3B, _9__3A, _8__3Y
endmodule

module SUBCIRCUIT_FOR_Y_Z (
  input  CS2,
  input  CS1,
  input  CS0,
  output Y_VAR,
  output Z
);

  wire n7408_1__3__1y, n74138_1__7__y7, n74138_1__9__y6, n74138_1__10__y5, n74138_1__11__y4,
       n74138_1__12__y3, n74138_1__13__y2, n74138_1__14__y1, n74138_1__15__y0;

  _74138 u_74138_1 (
    ._1__A(CS0), ._2__B(CS1), ._3__C(CS2), ._4__G2A(1'b0), ._5__G2B(1'b0), ._6__G1(1'b1),
    ._7__Y7(n74138_1__7__y7), ._8__GND(1'b0), ._16__Vcc(1'b1), ._15__Y0(n74138_1__15__y0),
    ._14__Y1(n74138_1__14__y1), ._13__Y2(n74138_1__13__y2), ._12__Y3(n74138_1__12__y3),
    ._11__Y4(n74138_1__11__y4), ._10__Y5(n74138_1__10__y5), ._9__Y6(n74138_1__9__y6));
  _7408 u_7408_1 (
    ._1__1A(n74138_1__15__y0), ._2__1B(n74138_1__11__y4), ._3__1Y(n7408_1__3__1y), ._4__2A(n7408_1__3__1y),
    ._5__2B(n74138_1__7__y7), ._6__2Y(Y_VAR), ._7__GND(1'b0), ._14__Vcc(1'b1), ._13__4B(CS1), ._12__4A(CS0),
    ._11__4Y(Z));  // open: _10__3B, _9__3A, _8__3Y
endmodule

module DESIGNING_4_BIT_X_Y_WITH_Z (
  input  [3:0] A,
  input  [3:0] B,
  input  CS2,
  input  CS1,
  input  CS0,
  output X3,
  output X2,
  output X1,
  output X0,
  output Z,
  output Y3,
  output Y2,
  output Y1,
  output Y0
);

  wire n7404_1__4__2y, n7404_1__6__3y, n7404_1__8__4y, n7404_1__10__5y, n7404_1__12__6y,
       subcircuit_for_y_z_1_y_var;

  DETERMINATION_OF_X X (.CS2(CS2), .CS1(CS1), .CS0(CS0), .A(A[3]), .B(B[3]), .X(X3));
  DETERMINATION_OF_X X_2 (.CS2(CS2), .CS1(CS1), .CS0(CS0), .A(A[2]), .B(B[2]), .X(X2));
  DETERMINATION_OF_X X_3 (.CS2(CS2), .CS1(CS1), .CS0(CS0), .A(A[1]), .B(B[1]), .X(X1));
  _7404 u_7404_1 (
    ._3__2A(B[1]), ._4__2Y(n7404_1__4__2y), ._5__3A(B[0]), ._6__3Y(n7404_1__6__3y), ._7__GND(1'b0),
    ._14__Vcc(1'b1), ._13__6A(B[3]), ._12__6Y(n7404_1__12__6y), ._11__5A(B[2]), ._10__5Y(n7404_1__10__5y),
    ._9__4A(subcircuit_for_y_z_1_y_var), ._8__4Y(n7404_1__8__4y));  // open: _1__1A, _2__1Y
  DETERMINATION_OF_X X_4 (.CS2(CS2), .CS1(CS1), .CS0(CS0), .A(A[0]), .B(B[0]), .X(X0));
  SUBCIRCUIT_FOR_Y_Z subcircuit_for_y_z_1 (.CS2(CS2), .CS1(CS1), .CS0(CS0), .Y_VAR(subcircuit_for_y_z_1_y_var), .Z(Z));
  _7408 u_7408_1 (
    ._1__1A(n7404_1__8__4y), ._2__1B(n7404_1__12__6y), ._3__1Y(Y3), ._4__2A(n7404_1__8__4y),
    ._5__2B(n7404_1__10__5y), ._6__2Y(Y2), ._7__GND(1'b0), ._14__Vcc(1'b1), ._13__4B(n7404_1__8__4y),
    ._12__4A(n7404_1__4__2y), ._11__4Y(Y1), ._10__3B(n7404_1__8__4y), ._9__3A(n7404_1__6__3y), ._8__3Y(Y0));
endmodule

module Flag (
  input  A4,
  input  B4,
  input  Cout,
  input  [3:0] in_4,
  output C,
  output V,
  output Z,
  output S
);

  wire n7432_1__3__1y, n7432_1__6__2y, n7432_1__8__3y, n7486_1__3__1y, n7486_1__6__2y;

  _7432 u_7432_1 (
    ._1__1A(in_4[0]), ._2__1B(in_4[1]), ._3__1Y(n7432_1__3__1y), ._4__2A(n7432_1__3__1y), ._5__2B(in_4[2]),
    ._6__2Y(n7432_1__6__2y), ._7__GND(1'b0), ._14__Vcc(1'b1), ._10__3B(in_4[3]), ._9__3A(n7432_1__6__2y),
    ._8__3Y(n7432_1__8__3y));  // open: _13__4B, _12__4A, _11__4Y
  _7486 u_7486_1 (
    ._1__1A(Cout), ._2__1B(B4), ._3__1Y(n7486_1__3__1y), ._4__2A(n7486_1__3__1y), ._5__2B(A4),
    ._6__2Y(n7486_1__6__2y), ._7__GND(1'b0), ._14__Vcc(1'b1), ._13__4B(n7486_1__6__2y), ._12__4A(in_4[3]),
    ._11__4Y(V));  // open: _10__3B, _9__3A, _8__3Y
  _7404 u_7404_1 (
    ._5__3A(n7432_1__8__3y), ._6__3Y(Z), ._7__GND(1'b0), ._14__Vcc(1'b1));  // open: _1__1A, _2__1Y, _3__2A, _4__2Y, _13__6A, _12__6Y, _11__5A, _10__5Y, _9__4A, _8__4Y

  assign C = Cout;
  assign S = in_4[3];
endmodule
