// Logisim project BIG ALU.circ as structural Verilog: 8 circuits, main circuit main
module main (
  input  A4,
  input  A3,
  input  A2,
  input  A1,
  input  Cin,
  output Cout,
  output S1,
  output S2,
  output S3,
  output S4
);

  BIG_ALU big_alu_1 ();  // open: SA, A32, A31, A30, A29, A28, A27, A26, A25, A24, A23, A22, A21, A20, A19, A18, A17, A16, A15, A14, A13, SB, B32, B31, B30, B29, B28, B27, B26, B25, B24, B23, B22, B21, B20, B19, B18, B17, B16, B15, B14, B13, A12, A11, A10, A9, A8, A7, A6, A5, A4, A3, A2, A1, B12, B11, B10, B9, B8, B7, B6, B5, B4, B3, B2, B1, C, S, OV, O32, O31, O30, O29, O28, O27, O26, O25, O24, O23, O22, O21, O20, O19, O18, O17, O16, O15, O14, O13, O12, O11, O10, O9, O8, O7, O6, O5, O4, O3, O2, O1
  _7483 u_7483_1 (
    ._1__A4(A4), ._2__S3(S3), ._3__A3(A3), ._4__B3(1'b0), ._5__Vcc(1'b1), ._6__S2(S2), ._7__B2(1'b0),
    ._8__A2(A2), ._16__B4(1'b0), ._15__S4(S4), ._14_Cout(Cout), ._13__Cin(Cin), ._12__GND(1'b0),
    ._11__B1(1'b0), ._10__A1(A1), ._9__S1(S1));
endmodule

module BIG_ALU_prestep (
  input  S,
  input  F20,
  input  F19,
  input  F18,
  input  F17,
  input  F16,
  input  F15,
  input  F14,
  input  F13,
  input  F12,
  input  F11,
  input  F10,
  input  F9,
  input  F8,
  input  F7,
  input  F6,
  input  F5,
  input  F4,
  input  F3,
  input  F2,
  input  O,
  input  F1,
  output out_23,
  output out_24,
  output out_25,
  output out_26,
  output out_27,
  output out_28,
  output out_29,
  output out_30,
  output out_31,
  output out_32,
  output out_33,
  output out_34,
  output out_35,
  output out_36,
  output out_37,
  output out_38,
  output out_39,
  output out_40,
  output out_41,
  output out_42,
  output out_43
);

  wire n2_scomplement_4_bit_adder_2_cout, n2_scomplement_4_bit_adder_3_cout,
       n2_scomplement_4_bit_adder_4_cout, n2_scomplement_4_bit_adder_5_cout, xor_1_out, xor_2_out, xor_3_out,
       xor_4_out, xor_5_out, xor_6_out, xor_7_out, xor_8_out, xor_9_out, xor_10_out, xor_11_out, xor_12_out,
       xor_13_out, xor_14_out, xor_15_out, xor_16_out, xor_17_out, xor_18_out, xor_19_out, xor_20_out;

  xor xor_1 (xor_1_out, S, F20);
  xor xor_2 (xor_2_out, S, F19);
  xor xor_3 (xor_3_out, S, F18);
  xor xor_4 (xor_4_out, S, F17);
  xor xor_5 (xor_5_out, S, F16);
  xor xor_6 (xor_6_out, S, F15);
  xor xor_7 (xor_7_out, S, F14);
  xor xor_8 (xor_8_out, S, F13);
  xor xor_9 (xor_9_out, S, F12);
  xor xor_10 (xor_10_out, S, F11);
  xor xor_11 (xor_11_out, S, F10);
  xor xor_12 (xor_12_out, S, F9);
  xor xor_13 (xor_13_out, S, F8);
  xor xor_14 (xor_14_out, S, F7);
  xor xor_15 (xor_15_out, S, F6);
  xor xor_16 (xor_16_out, S, F5);
  xor xor_17 (xor_17_out, S, F4);
  xor xor_18 (xor_18_out, S, F3);
  xor xor_19 (xor_19_out, S, F2);
  xor xor_20 (xor_20_out, S, F1);
  _2_scomplement_4_bit_adder u_2_scomplement_4_bit_adder_1 (
    .A4(xor_1_out), .A3(xor_2_out), .A2(xor_3_out), .A1(xor_4_out), .Cout(out_23), .S4(out_24), .S3(out_25),
    .S2(out_26), .S1(out_27), .Cin(n2_scomplement_4_bit_adder_2_cout));
  _2_scomplement_4_bit_adder u_2_scomplement_4_bit_adder_2 (
    .A4(xor_5_out), .A3(xor_6_out), .A2(xor_7_out), .A1(xor_8_out), .Cout(n2_scomplement_4_bit_adder_2_cout),
    .S4(out_28), .S3(out_29), .S2(out_30), .S1(out_31), .Cin(n2_scomplement_4_bit_adder_3_cout));
  _2_scomplement_4_bit_adder u_2_scomplement_4_bit_adder_3 (
    .A4(xor_9_out), .A3(xor_10_out), .A2(xor_11_out), .A1(xor_12_out),
    .Cout(n2_scomplement_4_bit_adder_3_cout), .S4(out_32), .S3(out_33), .S2(out_34), .S1(out_35),
    .Cin(n2_scomplement_4_bit_adder_4_cout));
  _2_scomplement_4_bit_adder u_2_scomplement_4_bit_adder_4 (
    .A4(xor_13_out), .A3(xor_14_out), .A2(xor_15_out), .A1(xor_16_out),
    .Cout(n2_scomplement_4_bit_adder_4_cout), .S4(out_36), .S3(out_37), .S2(out_38), .S1(out_39),
    .Cin(n2_scomplement_4_bit_adder_5_cout));
  _2_scomplement_4_bit_adder u_2_scomplement_4_bit_adder_5 (
    .A4(xor_17_out), .A3(xor_18_out), .A2(xor_19_out), .A1(xor_20_out),
    .Cout(n2_scomplement_4_bit_adder_5_cout), .S4(out_40), .S3(out_41), .S2(out_42), .S1(out_43), .Cin(O));
endmodule

module _2_scomplement_4_bit_adder (
  input  A4,
  input  A3,
  input  A2,
  input  A1,
  input  Cin,
  output Cout,
  output S4,
  output S3,
  output S2,
  output S1
);

  _7483 u_7483_1 (
    ._1__A4(A4), ._2__S3(S3), ._3__A3(A3), ._4__B3(1'b0), ._5__Vcc(1'b1), ._6__S2(S2), ._7__B2(1'b0),
    ._8__A2(A2), ._16__B4(1'b0), ._15__S4(S4), ._14_Cout(Cout), ._13__Cin(Cin), ._12__GND(1'b0),
    ._11__B1(1'b0), ._10__A1(A1), ._9__S1(S1));
endmodule

module ADD_FIRST_20_BIT (
  input  SA,
  input  A20,
  input  A19,
  input  A18,
  input  A17,
  input  A16,
  input  A15,
  input  A14,
  input  A13,
  input  A12,
  input  A11,
  input  A10,
  input  A9,
  input  A8,
  input  A7,
  input  OA,
  input  A6,
  input  A5,
  input  A4,
  input  A3,
  input  A2,
  input  A1,
  input  SB,
  input  C_in,
  input  B20,
  input  B19,
  input  B18,
  input  B17,
  input  B16,
  input  B15,
  input  _2_s_IN,
  input  B14,
  input  B13,
  input  B12,
  input  B11,
  input  B10,
  input  B9,
  input  B8,
  input  OB,
  input  B7,
  input  B6,
  input  B5,
  input  B4,
  input  B3,
  input  B2,
  input  B1,
  output C,
  output S,
  output OV,
  output F20,
  output F19,
  output F18,
  output F17,
  output F16,
  output F15,
  output F14,
  output F13,
  output F12,
  output F11,
  output F10,
  output F9,
  output F8,
  output F7,
  output F6,
  output F5,
  output F4,
  output F3,
  output F2,
  output F1
);

  wire big_alu_prestep_1_out_24, big_alu_prestep_1_out_25, big_alu_prestep_1_out_26,
       big_alu_prestep_1_out_27, big_alu_prestep_1_out_28, big_alu_prestep_1_out_29,
       big_alu_prestep_1_out_30, big_alu_prestep_1_out_31, big_alu_prestep_1_out_32,
       big_alu_prestep_1_out_33, big_alu_prestep_1_out_34, big_alu_prestep_1_out_35,
       big_alu_prestep_1_out_36, big_alu_prestep_1_out_37, big_alu_prestep_1_out_38,
       big_alu_prestep_1_out_39, big_alu_prestep_1_out_40, big_alu_prestep_1_out_41,
       big_alu_prestep_1_out_42, big_alu_prestep_1_out_43, big_alu_prestep_2_out_24,
       big_alu_prestep_2_out_25, big_alu_prestep_2_out_26, big_alu_prestep_2_out_27,
       big_alu_prestep_2_out_28, big_alu_prestep_2_out_29, big_alu_prestep_2_out_30,
       big_alu_prestep_2_out_31, big_alu_prestep_2_out_32, big_alu_prestep_2_out_33,
       big_alu_prestep_2_out_34, big_alu_prestep_2_out_35, big_alu_prestep_2_out_36,
       big_alu_prestep_2_out_37, big_alu_prestep_2_out_38, big_alu_prestep_2_out_39,
       big_alu_prestep_2_out_40, big_alu_prestep_2_out_41, big_alu_prestep_2_out_42,
       big_alu_prestep_2_out_43, big_alu_prestep_3_out_23, multiplexer_3_out, n4_bit_adder_1_cout,
       n4_bit_adder_1_s1, n4_bit_adder_1_s2, n4_bit_adder_1_s3, n4_bit_adder_1_s4, n4_bit_adder_2_cout,
       n4_bit_adder_2_s1, n4_bit_adder_2_s2, n4_bit_adder_2_s3, n4_bit_adder_2_s4, n12_bit_adder_1_c_bit,
       n12_bit_adder_1_s1, n12_bit_adder_1_s2, n12_bit_adder_1_s3, n12_bit_adder_1_s4, n12_bit_adder_1_s5,
       n12_bit_adder_1_s6, n12_bit_adder_1_s7, n12_bit_adder_1_s8, n12_bit_adder_1_s9, n12_bit_adder_1_s10,
       n12_bit_adder_1_s11, n12_bit_adder_1_s12, not_1_out, xnor_1_out;
  wire [1:0] xor_2_out;

  BIG_ALU_prestep big_alu_prestep_1 (
    .S(SA), .F20(A20), .F19(A19), .F18(A18), .F17(A17), .F16(A16), .F15(A15), .F14(A14), .F13(A13),
    .F12(A12), .F11(A11), .F10(A10), .F9(A9), .F8(A8), .F7(A7), .F6(A6), .F5(A5), .F4(A4), .F3(A3), .F2(A2),
    .F1(A1), .O(OA), .out_24(big_alu_prestep_1_out_24), .out_25(big_alu_prestep_1_out_25),
    .out_26(big_alu_prestep_1_out_26), .out_27(big_alu_prestep_1_out_27), .out_28(big_alu_prestep_1_out_28),
    .out_29(big_alu_prestep_1_out_29), .out_30(big_alu_prestep_1_out_30), .out_31(big_alu_prestep_1_out_31),
    .out_32(big_alu_prestep_1_out_32), .out_33(big_alu_prestep_1_out_33), .out_34(big_alu_prestep_1_out_34),
    .out_35(big_alu_prestep_1_out_35), .out_36(big_alu_prestep_1_out_36), .out_37(big_alu_prestep_1_out_37),
    .out_38(big_alu_prestep_1_out_38), .out_39(big_alu_prestep_1_out_39), .out_40(big_alu_prestep_1_out_40),
    .out_41(big_alu_prestep_1_out_41), .out_42(big_alu_prestep_1_out_42), .out_43(big_alu_prestep_1_out_43));  // open: out_23
  BIG_ALU_prestep big_alu_prestep_2 (
    .S(SB), .F20(B20), .F19(B19), .F18(B18), .F17(B17), .F16(B16), .F15(B15), .F14(B14), .F13(B13),
    .F12(B12), .F11(B11), .F10(B10), .F9(B9), .F8(B8), .F7(B7), .F6(B6), .F5(B5), .F4(B4), .F3(B3), .F2(B2),
    .F1(B1), .O(OB), .out_24(big_alu_prestep_2_out_24), .out_25(big_alu_prestep_2_out_25),
    .out_26(big_alu_prestep_2_out_26), .out_27(big_alu_prestep_2_out_27), .out_28(big_alu_prestep_2_out_28),
    .out_29(big_alu_prestep_2_out_29), .out_30(big_alu_prestep_2_out_30), .out_31(big_alu_prestep_2_out_31),
    .out_32(big_alu_prestep_2_out_32), .out_33(big_alu_prestep_2_out_33), .out_34(big_alu_prestep_2_out_34),
    .out_35(big_alu_prestep_2_out_35), .out_36(big_alu_prestep_2_out_36), .out_37(big_alu_prestep_2_out_37),
    .out_38(big_alu_prestep_2_out_38), .out_39(big_alu_prestep_2_out_39), .out_40(big_alu_prestep_2_out_40),
    .out_41(big_alu_prestep_2_out_41), .out_42(big_alu_prestep_2_out_42), .out_43(big_alu_prestep_2_out_43));  // open: out_23
  _4_bit_Adder u_4_bit_adder_1 (
    .Cout(n4_bit_adder_1_cout), .A4(big_alu_prestep_1_out_24), .A3(big_alu_prestep_1_out_25),
    .A2(big_alu_prestep_1_out_26), .A1(big_alu_prestep_1_out_27), .B4(big_alu_prestep_2_out_24),
    .B3(big_alu_prestep_2_out_25), .B2(big_alu_prestep_2_out_26), .B1(big_alu_prestep_2_out_27),
    .Cin(n4_bit_adder_2_cout), .S1(n4_bit_adder_1_s1), .S2(n4_bit_adder_1_s2), .S3(n4_bit_adder_1_s3),
    .S4(n4_bit_adder_1_s4));
  xor xor_1 (xor_2_out[1], SA, SB);
  xor xor_2 (xor_2_out[0], SB, n4_bit_adder_1_cout);
  not not_1 (not_1_out, n4_bit_adder_1_cout);
  _4_bit_Adder u_4_bit_adder_2 (
    .Cout(n4_bit_adder_2_cout), .A4(big_alu_prestep_1_out_28), .A3(big_alu_prestep_1_out_29),
    .A2(big_alu_prestep_1_out_30), .A1(big_alu_prestep_1_out_31), .B4(big_alu_prestep_2_out_28),
    .B3(big_alu_prestep_2_out_29), .B2(big_alu_prestep_2_out_30), .B1(big_alu_prestep_2_out_31),
    .Cin(n12_bit_adder_1_c_bit), .S1(n4_bit_adder_2_s1), .S2(n4_bit_adder_2_s2), .S3(n4_bit_adder_2_s3),
    .S4(n4_bit_adder_2_s4));
  _12_bit_adder u_12_bit_adder_1 (
    .Cin(C_in), .A12(big_alu_prestep_1_out_32), .A11(big_alu_prestep_1_out_33),
    .A10(big_alu_prestep_1_out_34), .A9(big_alu_prestep_1_out_35), .A8(big_alu_prestep_1_out_36),
    .A7(big_alu_prestep_1_out_37), .A6(big_alu_prestep_1_out_38), .A5(big_alu_prestep_1_out_39),
    .A4(big_alu_prestep_1_out_40), .A3(big_alu_prestep_1_out_41), .A2(big_alu_prestep_1_out_42),
    .A1(big_alu_prestep_1_out_43), .B12(big_alu_prestep_2_out_32), .B11(big_alu_prestep_2_out_33),
    .B10(big_alu_prestep_2_out_34), .B9(big_alu_prestep_2_out_35), .B8(big_alu_prestep_2_out_36),
    .B7(big_alu_prestep_2_out_37), .B6(big_alu_prestep_2_out_38), .B5(big_alu_prestep_2_out_39),
    .B4(big_alu_prestep_2_out_40), .B3(big_alu_prestep_2_out_41), .B2(big_alu_prestep_2_out_42),
    .B1(big_alu_prestep_2_out_43), .C_Bit(n12_bit_adder_1_c_bit), .S12(n12_bit_adder_1_s12),
    .S11(n12_bit_adder_1_s11), .S10(n12_bit_adder_1_s10), .S9(n12_bit_adder_1_s9), .S8(n12_bit_adder_1_s8),
    .S7(n12_bit_adder_1_s7), .S6(n12_bit_adder_1_s6), .S5(n12_bit_adder_1_s5), .S4(n12_bit_adder_1_s4),
    .S3(n12_bit_adder_1_s3), .S2(n12_bit_adder_1_s2), .S1(n12_bit_adder_1_s1));
  Multiplexer #(.select(2)) multiplexer_1 (
    .in0(n4_bit_adder_1_cout), .in1(SA), .in2(not_1_out), .in3(not_1_out), .out(S), .sel(xor_2_out));  // open: en
  Multiplexer #(.select(2)) multiplexer_2 (
    .in0(1'b0), .in1(1'b1), .in2(1'b0), .in3(1'b0), .out(OV), .sel(xor_2_out));  // open: en
  Multiplexer multiplexer_3 (
    .in0(n4_bit_adder_1_cout), .in1(xnor_1_out), .out(multiplexer_3_out), .sel(S));  // open: en
  BIG_ALU_prestep big_alu_prestep_3 (
    .S(S), .F20(n4_bit_adder_1_s4), .F19(n4_bit_adder_1_s3), .F18(n4_bit_adder_1_s2),
    .F17(n4_bit_adder_1_s1), .F16(n4_bit_adder_2_s4), .F15(n4_bit_adder_2_s3), .F14(n4_bit_adder_2_s2),
    .F13(n4_bit_adder_2_s1), .F12(n12_bit_adder_1_s12), .F11(n12_bit_adder_1_s11), .F10(n12_bit_adder_1_s10),
    .F9(n12_bit_adder_1_s9), .F8(n12_bit_adder_1_s8), .F7(n12_bit_adder_1_s7), .F6(n12_bit_adder_1_s6),
    .F5(n12_bit_adder_1_s5), .F4(n12_bit_adder_1_s4), .F3(n12_bit_adder_1_s3), .F2(n12_bit_adder_1_s2),
    .F1(n12_bit_adder_1_s1), .O(_2_s_IN), .out_23(big_alu_prestep_3_out_23), .out_24(F20), .out_25(F19),
    .out_26(F18), .out_27(F17), .out_28(F16), .out_29(F15), .out_30(F14), .out_31(F13), .out_32(F12),
    .out_33(F11), .out_34(F10), .out_35(F9), .out_36(F8), .out_37(F7), .out_38(F6), .out_39(F5), .out_40(F4),
    .out_41(F3), .out_42(F2), .out_43(F1));
  Multiplexer multiplexer_4 (.in0(multiplexer_3_out), .in1(1'b0), .out(C), .sel(xor_2_out[1]));  // open: en
  xnor xnor_1 (xnor_1_out, big_alu_prestep_3_out_23, n4_bit_adder_1_cout);
endmodule

module _4_bit_Adder (
  input  A4,
  input  A3,
  input  A2,
  input  A1,
  input  Cin,
  input  B4,
  input  B3,
  input  B2,
  input  B1,
  output Cout,
  output S1,
  output S2,
  output S3,
  output S4
);

  _7483 u_7483_1 (
    ._1__A4(A4), ._2__S3(S3), ._3__A3(A3), ._4__B3(B3), ._5__Vcc(1'b1), ._6__S2(S2), ._7__B2(B2),
    ._8__A2(A2), ._16__B4(B4), ._15__S4(S4), ._14_Cout(Cout), ._13__Cin(Cin), ._12__GND(1'b0), ._11__B1(B1),
    ._10__A1(A1), ._9__S1(S1));
endmodule

module _12_bit_adder (
  input  A12,
  input  A11,
  input  A10,
  input  A9,
  input  A8,
  input  A7,
  input  A6,
  input  A5,
  input  A4,
  input  A3,
  input  A2,
  input  A1,
  input  Cin,
  input  B12,
  input  B11,
  input  B10,
  input  B9,
  input  B8,
  input  B7,
  input  B6,
  input  B5,
  input  B4,
  input  B3,
  input  B2,
  input  B1,
  output C_Bit,
  output S12,
  output S11,
  output S10,
  output S9,
  output S8,
  output S7,
  output S6,
  output S5,
  output S4,
  output S3,
  output S2,
  output S1
);

  wire n4_bit_adder_2_cout, n4_bit_adder_3_cout;

  _4_bit_Adder u_4_bit_adder_1 (
    .Cout(C_Bit), .A4(A12), .A3(A11), .A2(A10), .A1(A9), .B4(B12), .B3(B11), .B2(B10), .B1(B9),
    .Cin(n4_bit_adder_2_cout), .S1(S9), .S2(S10), .S3(S11), .S4(S12));
  _4_bit_Adder u_4_bit_adder_2 (
    .Cout(n4_bit_adder_2_cout), .A4(A8), .A3(A7), .A2(A6), .A1(A5), .B4(B8), .B3(B7), .B2(B6), .B1(B5),
    .Cin(n4_bit_adder_3_cout), .S1(S5), .S2(S6), .S3(S7), .S4(S8));
  _4_bit_Adder u_4_bit_adder_3 (
    .Cout(n4_bit_adder_3_cout), .A4(A4), .A3(A3), .A2(A2), .A1(A1), .B4(B4), .B3(B3), .B2(B2), .B1(B1),
    .Cin(Cin), .S1(S1), .S2(S2), .S3(S3), .S4(S4));
endmodule

module BIG_ALU (
  input  A12,
  input  A11,
  input  A10,
  input  A9,
  input  A8,
  input  A7,
  input  A6,
  input  A5,
  input  A4,
  input  A3,
  input  A2,
  input  A1,
  input  SA,
  input  A32,
  input  A31,
  input  A30,
  input  A29,
  input  A28,
  input  A27,
  input  A26,
  input  A25,
  input  A24,
  input  A23,
  input  A22,
  input  B12,
  input  B11,
  input  B10,
  input  B9,
  input  B8,
  input  B7,
  input  B6,
  input  B5,
  input  B4,
  input  B3,
  input  B2,
  input  B1,
  input  A21,
  input  A20,
  input  A19,
  input  A18,
  input  A17,
  input  A16,
  input  A15,
  input  A14,
  input  A13,
  input  SB,
  input  B32,
  input  B31,
  input  B30,
  input  B29,
  input  B28,
  input  B27,
  input  B26,
  input  B25,
  input  B24,
  input  B23,
  input  B22,
  input  B21,
  input  B20,
  input  B19,
  input  B18,
  input  B17,
  input  B16,
  input  B15,
  input  B14,
  input  B13,
  output C,
  output S,
  output OV,
  output O32,
  output O31,
  output O30,
  output O29,
  output O28,
  output O27,
  output O26,
  output O25,
  output O24,
  output O23,
  output O22,
  output O21,
  output O20,
  output O19,
  output O18,
  output O17,
  output O16,
  output O15,
  output O14,
  output O13,
  output O12,
  output O11,
  output O10,
  output O9,
  output O8,
  output O7,
  output O6,
  output O5,
  output O4,
  output O3,
  output O2,
  output O1
);

  wire big_alu_prestep_1_out_23, n12_bit_adder_subtractor_1_oa, n12_bit_adder_subtractor_1_ob,
       n12_bit_adder_subtractor_1_out_28;
  wire [11:0] n12_bit_adder_subtractor_1_out_41;

  _12_bit_adder_subtractor u_12_bit_adder_subtractor_1 (
    .OA(n12_bit_adder_subtractor_1_oa), .SA(SA), .OB(n12_bit_adder_subtractor_1_ob), .SB(SB), .A12(A12),
    .A11(A11), .A10(A10), .A9(A9), .A8(A8), .A7(A7), .A6(A6), .A5(A5), .A4(A4), .A3(A3), .A2(A2), .A1(A1),
    .B12(B12), .B11(B11), .B10(B10), .B9(B9), .B8(B8), .B7(B7), .B6(B6), .B5(B5), .B4(B4), .B3(B3), .B2(B2),
    .B1(B1), .out_28(n12_bit_adder_subtractor_1_out_28), .out_29(n12_bit_adder_subtractor_1_out_41[11]),
    .out_30(n12_bit_adder_subtractor_1_out_41[10]), .out_31(n12_bit_adder_subtractor_1_out_41[9]),
    .out_32(n12_bit_adder_subtractor_1_out_41[8]), .out_34(n12_bit_adder_subtractor_1_out_41[7]),
    .out_35(n12_bit_adder_subtractor_1_out_41[6]), .out_36(n12_bit_adder_subtractor_1_out_41[5]),
    .out_37(n12_bit_adder_subtractor_1_out_41[4]), .out_38(n12_bit_adder_subtractor_1_out_41[3]),
    .out_39(n12_bit_adder_subtractor_1_out_41[2]), .out_40(n12_bit_adder_subtractor_1_out_41[1]),
    .out_41(n12_bit_adder_subtractor_1_out_41[0]));
  BIG_ALU_prestep big_alu_prestep_1 (
    .S(S), .F20(1'b0), .F19(1'b0), .F18(1'b0), .F17(1'b0), .F16(1'b0), .F15(1'b0), .F14(1'b0), .F13(1'b0),
    .F12(n12_bit_adder_subtractor_1_out_41[11]), .F11(n12_bit_adder_subtractor_1_out_41[10]),
    .F10(n12_bit_adder_subtractor_1_out_41[9]), .F9(n12_bit_adder_subtractor_1_out_41[8]),
    .F8(n12_bit_adder_subtractor_1_out_41[7]), .F7(n12_bit_adder_subtractor_1_out_41[6]),
    .F6(n12_bit_adder_subtractor_1_out_41[5]), .F5(n12_bit_adder_subtractor_1_out_41[4]),
    .F4(n12_bit_adder_subtractor_1_out_41[3]), .F3(n12_bit_adder_subtractor_1_out_41[2]),
    .F2(n12_bit_adder_subtractor_1_out_41[1]), .F1(n12_bit_adder_subtractor_1_out_41[0]), .O(S),
    .out_23(big_alu_prestep_1_out_23), .out_32(O12), .out_33(O11), .out_34(O10), .out_35(O9), .out_36(O8),
    .out_37(O7), .out_38(O6), .out_39(O5), .out_40(O4), .out_41(O3), .out_42(O2), .out_43(O1));  // open: out_24, out_25, out_26, out_27, out_28, out_29, out_30, out_31
  ADD_FIRST_20_BIT add_first_20_bit_1 (
    .SA(SA), .A20(A32), .A19(A31), .A18(A30), .A17(A29), .A16(A28), .A15(A27), .A14(A26), .A13(A25),
    .A12(A24), .A11(A23), .A10(A22), .A9(A21), .A8(A20), .A7(A19), .A6(A18), .A5(A17), .A4(A16), .A3(A15),
    .A2(A14), .A1(A13), .SB(SB), .B20(B32), .B19(B31), .B18(B30), .B17(B29), .B16(B28), .B15(B27), .B14(B26),
    .B13(B25), .B12(B24), .B11(B23), .B10(B22), .B9(B21), .B8(B20), .B7(B19), .B6(B18), .B5(B17), .B4(B16),
    .B3(B15), .B2(B14), .B1(B13), .C_in(n12_bit_adder_subtractor_1_out_28),
    .OB(n12_bit_adder_subtractor_1_ob), .OA(n12_bit_adder_subtractor_1_oa),
    ._2_s_IN(big_alu_prestep_1_out_23), .C(C), .S(S), .OV(OV), .F20(O32), .F19(O31), .F18(O30), .F17(O29),
    .F16(O28), .F15(O27), .F14(O26), .F13(O25), .F12(O24), .F11(O23), .F10(O22), .F9(O21), .F8(O20),
    .F7(O19), .F6(O18), .F5(O17), .F4(O16), .F3(O15), .F2(O14), .F1(O13));
endmodule

module _12_bit_adder_subtractor (
  input  A12,
  input  A11,
  input  A10,
  input  A9,
  input  A8,
  input  A7,
  input  A6,
  input  A5,
  input  A4,
  input  A3,
  input  A2,
  input  A1,
  input  SA,
  input  SB,
  input  B12,
  input  B11,
  input  B10,
  input  B9,
  input  B8,
  input  B7,
  input  B6,
  input  B5,
  input  B4,
  input  B3,
  input  B2,
  input  B1,
  output OA,
  output out_28,
  output out_29,
  output out_30,
  output out_31,
  output out_32,
  output OB,
  output out_34,
  output out_35,
  output out_36,
  output out_37,
  output out_38,
  output out_39,
  output out_40,
  output out_41
);

  wire big_alu_prestep_1_out_32, big_alu_prestep_1_out_33, big_alu_prestep_1_out_34,
       big_alu_prestep_1_out_35, big_alu_prestep_1_out_36, big_alu_prestep_1_out_37,
       big_alu_prestep_1_out_38, big_alu_prestep_1_out_39, big_alu_prestep_1_out_40,
       big_alu_prestep_1_out_41, big_alu_prestep_1_out_42, big_alu_prestep_1_out_43;
  wire [11:0] big_alu_prestep_2_out_43;

  BIG_ALU_prestep big_alu_prestep_1 (
    .S(SB), .F20(1'b0), .F19(1'b0), .F18(1'b0), .F17(1'b0), .F16(1'b0), .F15(1'b0), .F14(1'b0), .F13(1'b0),
    .F12(B12), .F11(B11), .F10(B10), .F9(B9), .F8(B8), .F7(B7), .F6(B6), .F5(B5), .F4(B4), .F3(B3), .F2(B2),
    .F1(B1), .O(SB), .out_23(OB), .out_32(big_alu_prestep_1_out_32), .out_33(big_alu_prestep_1_out_33),
    .out_34(big_alu_prestep_1_out_34), .out_35(big_alu_prestep_1_out_35), .out_36(big_alu_prestep_1_out_36),
    .out_37(big_alu_prestep_1_out_37), .out_38(big_alu_prestep_1_out_38), .out_39(big_alu_prestep_1_out_39),
    .out_40(big_alu_prestep_1_out_40), .out_41(big_alu_prestep_1_out_41), .out_42(big_alu_prestep_1_out_42),
    .out_43(big_alu_prestep_1_out_43));  // open: out_24, out_25, out_26, out_27, out_28, out_29, out_30, out_31
  _12_bit_adder u_12_bit_adder_1 (
    .Cin(1'b0), .A12(big_alu_prestep_2_out_43[11]), .A11(big_alu_prestep_2_out_43[10]),
    .A10(big_alu_prestep_2_out_43[9]), .A9(big_alu_prestep_2_out_43[8]), .A8(big_alu_prestep_2_out_43[7]),
    .A7(big_alu_prestep_2_out_43[6]), .A6(big_alu_prestep_2_out_43[5]), .A5(big_alu_prestep_2_out_43[4]),
    .A4(big_alu_prestep_2_out_43[3]), .A3(big_alu_prestep_2_out_43[2]), .A2(big_alu_prestep_2_out_43[1]),
    .A1(big_alu_prestep_2_out_43[0]), .B12(big_alu_prestep_1_out_32), .B11(big_alu_prestep_1_out_33),
    .B10(big_alu_prestep_1_out_34), .B9(big_alu_prestep_1_out_35), .B8(big_alu_prestep_1_out_36),
    .B7(big_alu_prestep_1_out_37), .B6(big_alu_prestep_1_out_38), .B5(big_alu_prestep_1_out_39),
    .B4(big_alu_prestep_1_out_40), .B3(big_alu_prestep_1_out_41), .B2(big_alu_prestep_1_out_42),
    .B1(big_alu_prestep_1_out_43), .C_Bit(out_28), .S12(out_29), .S11(out_30), .S10(out_31), .S9(out_32),
    .S8(out_34), .S7(out_35), .S6(out_36), .S5(out_37), .S4(out_38), .S3(out_39), .S2(out_40), .S1(out_41));
  BIG_ALU_prestep big_alu_prestep_2 (
    .S(SA), .F20(1'b0), .F19(1'b0), .F18(1'b0), .F17(1'b0), .F16(1'b0), .F15(1'b0), .F14(1'b0), .F13(1'b0),
    .F12(A12), .F11(A11), .F10(A10), .F9(A9), .F8(A8), .F7(A7), .F6(A6), .F5(A5), .F4(A4), .F3(A3), .F2(A2),
    .F1(A1), .O(SA), .out_23(OA), .out_32(big_alu_prestep_2_out_43[11]),
    .out_33(big_alu_prestep_2_out_43[10]), .out_34(big_alu_prestep_2_out_43[9]),
    .out_35(big_alu_prestep_2_out_43[8]), .out_36(big_alu_prestep_2_out_43[7]),
    .out_37(big_alu_prestep_2_out_43[6]), .out_38(big_alu_prestep_2_out_43[5]),
    .out_39(big_alu_prestep_2_out_43[4]), .out_40(big_alu_prestep_2_out_43[3]),
    .out_41(big_alu_prestep_2_out_43[2]), .out_42(big_alu_prestep_2_out_43[1]),
    .out_43(big_alu_prestep_2_out_43[0]));  // open: out_24, out_25, out_26, out_27, out_28, out_29, out_30, out_31
endmodule
