// Logisim project SMALL NUMBER RIGHT SHIFT.circ as structural Verilog
// SHIFTER(R)(SF)
module SHIFTER (
  input  F19,
  input  F18,
  input  F17,
  input  F16,
  input  F15,
  input  F14,
  input  F13,
  input  F12,
  input  F11,
  input  F10,
  input  F9,
  input  F8,
  input  F7,
  input  F6,
  input  F5,
  input  F4,
  input  F3,
  input  F2,
  input  F1,
  input  E12,
  input  E11,
  input  E10,
  input  E09,
  input  E08,
  input  E07,
  input  E06,
  input  E05,
  input  E04,
  input  E03,
  input  E02,
  input  E01,
  output O32,
  output O31,
  output O30,
  output O29,
  output O28,
  output O27,
  output O26,
  output O25,
  output O24,
  output O23,
  output O22,
  output O21,
  output O20,
  output O19,
  output O18,
  output O17,
  output O16,
  output O15,
  output O14,
  output O13,
  output O12,
  output O11,
  output O10,
  output O9,
  output O8,
  output O7,
  output O6,
  output O5,
  output O4,
  output O3,
  output O2,
  output O1
);

  wire [4:0] exponent_trigger_1_t1;

  EXPONENT_TRIGGER exponent_trigger_1 (
    .E12(E12), .E11(E11), .E10(E10), .E09(E09), .E08(E08), .E07(E07), .E06(E06), .E05(E05), .E04(E04),
    .E03(E03), .E02(E02), .E01(E01), .T5(exponent_trigger_1_t1[4]), .T4(exponent_trigger_1_t1[3]),
    .T3(exponent_trigger_1_t1[2]), .T2(exponent_trigger_1_t1[1]), .T1(exponent_trigger_1_t1[0]));
  Shifter #(.width(32), .shift("lr")) shifter_1 (
    .in({1'b1, F19, F18, F17, F16, F15, F14, F13, F12, F11, F10, F9, F8, F7, F6, F5, F4, F3, F2, F1, {12{1'b0}}}),
    .\dist (exponent_trigger_1_t1),
    .out({O32, O31, O30, O29, O28, O27, O26, O25, O24, O23, O22, O21, O20, O19, O18, O17, O16, O15, O14, O13, O12, O11, O10, O9, O8, O7, O6, O5, O4, O3, O2, O1}));
endmodule

module EXPONENT_TRIGGER (
  input  E12,
  input  E11,
  input  E10,
  input  E09,
  input  E08,
  input  E07,
  input  E06,
  input  E05,
  input  E04,
  input  E03,
  input  E02,
  input  E01,
  output T5,
  output T4,
  output T3,
  output T2,
  output T1
);

  wire or_1_out, undriven, undriven_2, undriven_3;

  or or_1 (or_1_out, undriven, undriven_2, undriven_3);
  _74148 u_74148_1 (
    ._1__I4(E09), ._2__I5(E10), ._3__I6(E11), ._4__I7(E12), ._5__nEI__NC(1'b0), ._6__A2(undriven),
    ._7__A1(undriven_2), ._8__GND(1'b0), ._16__Vcc(1'b1), ._13__I3(E08), ._12__I2(E07), ._11__I1(E06),
    ._10__I0(1'b1), ._9__A0(undriven_3));  // open: _15__nEO__NC, _14__nGS__NC
  or or_2 (T5, E05, or_1_out);
  or or_3 (T4, E04, or_1_out);
  or or_4 (T3, E03, or_1_out);
  or or_5 (T2, E02, or_1_out);
  or or_6 (T1, E01, or_1_out);
endmodule
