// Logisim project SMALL ALU.circ as structural Verilog: 7 circuits, main circuit SMALL ALU 
// 12 BIT COMPARATOR
module _12_bit_Comparator (
  input  A12,
  input  A11,
  input  A10,
  input  A9,
  input  A8,
  input  A7,
  input  A6,
  input  A5,
  input  A4,
  input  A3,
  input  A2,
  input  A1,
  input  B12,
  input  B11,
  input  B10,
  input  B9,
  input  B8,
  input  B7,
  input  B6,
  input  B5,
  input  B4,
  input  B3,
  input  B2,
  input  B1,
  output A_B,
  output A_B_2,
  output A_B_3
);

  wire ic_7485_1_a_b, ic_7485_1_a_b_2, ic_7485_1_a_b_3, ic_7485_2_a_b, ic_7485_2_a_b_2, ic_7485_2_a_b_3;

  IC_7485 ic_7485_1 (
    .B3(B12), .EN_A_B(1'b0), .EN_A_B_2(1'b1), .EN_A_B_3(1'b0), .A_B(ic_7485_1_a_b), .A_B_2(ic_7485_1_a_b_2),
    .A_B_3(ic_7485_1_a_b_3), .GND(1'b0), .VCC(1'b1), .A3(A12), .B2(B11), .A2(A11), .A1(A10), .B1(B10),
    .A0(A9), .B0(B9));
  IC_7485 ic_7485_2 (
    .B3(B8), .EN_A_B(ic_7485_1_a_b_3), .EN_A_B_2(ic_7485_1_a_b_2), .EN_A_B_3(ic_7485_1_a_b),
    .A_B(ic_7485_2_a_b), .A_B_2(ic_7485_2_a_b_2), .A_B_3(ic_7485_2_a_b_3), .GND(1'b0), .VCC(1'b1), .A3(A8),
    .B2(B7), .A2(A7), .A1(A6), .B1(B6), .A0(A5), .B0(B5));
  IC_7485 ic_7485_3 (
    .B3(B4), .EN_A_B(ic_7485_2_a_b_3), .EN_A_B_2(ic_7485_2_a_b_2), .EN_A_B_3(ic_7485_2_a_b), .A_B(A_B),
    .A_B_2(A_B_2), .A_B_3(A_B_3), .GND(1'b0), .VCC(1'b1), .A3(A4), .B2(B3), .A2(A3), .A1(A2), .B1(B2),
    .A0(A1), .B0(B1));
endmodule

// 7485
module IC_7485 (
  input  B3,
  input  VCC,
  input  EN_A_B,
  input  A3,
  input  EN_A_B_2,
  input  B2,
  input  EN_A_B_3,
  input  A2,
  input  A1,
  input  B1,
  input  A0,
  input  GND,
  input  B0,
  output A_B,
  output A_B_2,
  output A_B_3
);

  wire and_1_out, and_2_out, and_4_out, comparator_1_eq, comparator_1_lt, comparator_2_eq, comparator_2_lt,
       comparator_3_eq, comparator_3_lt, comparator_4_eq, comparator_4_lt, not_1_out, or_1_out;

  Comparator #(.width(1)) comparator_1 (.a(A3), .b(B3), .eq(comparator_1_eq), .lt(comparator_1_lt));  // open: gt
  Comparator #(.width(1)) comparator_2 (.a(A2), .b(B2), .eq(comparator_2_eq), .lt(comparator_2_lt));  // open: gt
  Comparator #(.width(1)) comparator_3 (.a(A1), .b(B1), .eq(comparator_3_eq), .lt(comparator_3_lt));  // open: gt
  Comparator #(.width(1)) comparator_4 (.a(A0), .b(B0), .eq(comparator_4_eq), .lt(comparator_4_lt));  // open: gt
  and and_1 (and_1_out, comparator_1_eq, comparator_2_lt);
  and and_2 (and_2_out, comparator_1_eq, comparator_2_eq, comparator_3_lt);
  and and_3 (A_B_2, comparator_1_eq, comparator_2_eq, EN_A_B_2, comparator_3_eq, comparator_4_eq);
  and and_4 (and_4_out, comparator_1_eq, comparator_3_eq, comparator_2_eq, comparator_4_lt);
  not not_1 (not_1_out, EN_A_B);
  or or_1 (or_1_out, and_4_out, comparator_1_lt, EN_A_B_3, and_2_out, and_1_out);
  and and_5 (A_B, not_1_out, or_1_out);
  nor nor_1 (A_B_3, A_B, A_B_2);
endmodule

module _4_bit_adder (
  input  A4,
  input  A3,
  input  A2,
  input  A1,
  input  Cin,
  input  B4,
  input  B3,
  input  B2,
  input  B1,
  output Cout,
  output S1,
  output S2,
  output S3,
  output S4
);

  _7483 u_7483_1 (
    ._1__A4(A4), ._2__S3(S3), ._3__A3(A3), ._4__B3(B3), ._5__Vcc(1'b1), ._6__S2(S2), ._7__B2(B2),
    ._8__A2(A2), ._16__B4(B4), ._15__S4(S4), ._14_Cout(Cout), ._13__Cin(Cin), ._12__GND(1'b0), ._11__B1(B1),
    ._10__A1(A1), ._9__S1(S1));
endmodule

module _12_bit_adder (
  input  A12,
  input  A11,
  input  A10,
  input  A9,
  input  A8,
  input  A7,
  input  A6,
  input  A5,
  input  A4,
  input  A3,
  input  A2,
  input  A1,
  input  Cin,
  input  B12,
  input  B11,
  input  B10,
  input  B9,
  input  B8,
  input  B7,
  input  B6,
  input  B5,
  input  B4,
  input  B3,
  input  B2,
  input  B1,
  output C_Bit,
  output S12,
  output S11,
  output S10,
  output S9,
  output S8,
  output S7,
  output S6,
  output S5,
  output S4,
  output S3,
  output S2,
  output S1
);

  wire n4_bit_adder_2_cout, n4_bit_adder_3_cout;

  _4_bit_adder u_4_bit_adder_1 (
    .Cout(C_Bit), .A4(A12), .A3(A11), .A2(A10), .A1(A9), .B4(B12), .B3(B11), .B2(B10), .B1(B9),
    .Cin(n4_bit_adder_2_cout), .S1(S9), .S2(S10), .S3(S11), .S4(S12));
  _4_bit_adder u_4_bit_adder_2 (
    .Cout(n4_bit_adder_2_cout), .A4(A8), .A3(A7), .A2(A6), .A1(A5), .B4(B8), .B3(B7), .B2(B6), .B1(B5),
    .Cin(n4_bit_adder_3_cout), .S1(S5), .S2(S6), .S3(S7), .S4(S8));
  _4_bit_adder u_4_bit_adder_3 (
    .Cout(n4_bit_adder_3_cout), .A4(A4), .A3(A3), .A2(A2), .A1(A1), .B4(B4), .B3(B3), .B2(B2), .B1(B1),
    .Cin(Cin), .S1(S1), .S2(S2), .S3(S3), .S4(S4));
endmodule

module Adder_Test (
  input  A12,
  input  A11,
  input  A10,
  input  A9,
  input  A8,
  input  A7,
  input  A6,
  input  A5,
  input  A4,
  input  A3,
  input  A2,
  input  A1,
  input  B12,
  input  B11,
  input  B10,
  input  B9,
  input  B8,
  input  B7,
  input  B6,
  input  B5,
  input  B4,
  input  B3,
  input  B2,
  input  B1
);

  _12_bit_adder u_12_bit_adder_1 (
    .Cin(1'b0), .A12(A12), .A11(A11), .A10(A10), .A9(A9), .A8(A8), .A7(A7), .A6(A6), .A5(A5), .A4(A4),
    .A3(A3), .A2(A2), .A1(A1), .B12(B12), .B11(B11), .B10(B10), .B9(B9), .B8(B8), .B7(B7), .B6(B6), .B5(B5),
    .B4(B4), .B3(B3), .B2(B2), .B1(B1));  // open: C_Bit, S12, S11, S10, S9, S8, S7, S6, S5, S4, S3, S2, S1
endmodule

module SMALL_ALU_prestep (
  input  A12,
  input  A11,
  input  A10,
  input  A9,
  input  A8,
  input  A7,
  input  A6,
  input  A5,
  input  A4,
  input  A3,
  input  A2,
  input  A1,
  input  B12,
  input  B11,
  input  B10,
  input  B9,
  input  B8,
  input  B7,
  input  B6,
  input  B5,
  input  B4,
  input  B3,
  input  B2,
  input  B1,
  output E1_12,
  output E1_11,
  output E1_10,
  output E1_09,
  output E1_08,
  output E1_07,
  output E1_06,
  output E1_05,
  output E1_04,
  output E1_03,
  output E1_02,
  output E1_01,
  output E2_12,
  output E2_11,
  output E2_10,
  output E2_09,
  output E2_08,
  output E2_07,
  output E2_06,
  output E2_05,
  output E2_04,
  output E2_03,
  output E2_02,
  output E2_01
);

  wire n12_bit_comparator_1_a_b, n12_bit_comparator_1_a_b_2, n12_bit_comparator_1_a_b_3, or_1_out;

  _12_bit_Comparator u_12_bit_comparator_1 (
    .A12(A12), .A11(A11), .A10(A10), .A9(A9), .A8(A8), .A7(A7), .A6(A6), .A5(A5), .A4(A4), .A3(A3), .A2(A2),
    .A1(A1), .B12(B12), .B11(B11), .B10(B10), .B9(B9), .B8(B8), .B7(B7), .B6(B6), .B5(B5), .B4(B4), .B3(B3),
    .B2(B2), .B1(B1), .A_B(n12_bit_comparator_1_a_b), .A_B_2(n12_bit_comparator_1_a_b_2),
    .A_B_3(n12_bit_comparator_1_a_b_3));
  or or_1 (or_1_out, n12_bit_comparator_1_a_b, n12_bit_comparator_1_a_b_2);
  _7486 u_7486_1 (
    ._1__1A(n12_bit_comparator_1_a_b_3), ._2__1B(A12), ._3__1Y(E1_12), ._4__2A(n12_bit_comparator_1_a_b_3),
    ._5__2B(A11), ._6__2Y(E1_11), ._7__GND(1'b0), ._14__Vcc(1'b1), ._13__4B(A10),
    ._12__4A(n12_bit_comparator_1_a_b_3), ._11__4Y(E1_10), ._10__3B(n12_bit_comparator_1_a_b_3), ._9__3A(A9),
    ._8__3Y(E1_09));
  _7486 u_7486_2 (
    ._1__1A(n12_bit_comparator_1_a_b_3), ._2__1B(A8), ._3__1Y(E1_08), ._4__2A(n12_bit_comparator_1_a_b_3),
    ._5__2B(A7), ._6__2Y(E1_07), ._7__GND(1'b0), ._14__Vcc(1'b1), ._13__4B(A6),
    ._12__4A(n12_bit_comparator_1_a_b_3), ._11__4Y(E1_06), ._10__3B(A5), ._9__3A(n12_bit_comparator_1_a_b_3),
    ._8__3Y(E1_05));
  _7486 u_7486_3 (
    ._1__1A(n12_bit_comparator_1_a_b_3), ._2__1B(A4), ._3__1Y(E1_04), ._4__2A(A3),
    ._5__2B(n12_bit_comparator_1_a_b_3), ._6__2Y(E1_03), ._7__GND(1'b0), ._14__Vcc(1'b1), ._13__4B(A2),
    ._12__4A(n12_bit_comparator_1_a_b_3), ._11__4Y(E1_02), ._10__3B(A1), ._9__3A(n12_bit_comparator_1_a_b_3),
    ._8__3Y(E1_01));
  _7486 u_7486_4 (
    ._1__1A(B12), ._2__1B(or_1_out), ._3__1Y(E2_12), ._4__2A(or_1_out), ._5__2B(B11), ._6__2Y(E2_11),
    ._7__GND(1'b0), ._14__Vcc(1'b1), ._13__4B(B10), ._12__4A(or_1_out), ._11__4Y(E2_10), ._10__3B(or_1_out),
    ._9__3A(B9), ._8__3Y(E2_09));
  _7486 u_7486_5 (
    ._1__1A(B8), ._2__1B(or_1_out), ._3__1Y(E2_08), ._4__2A(B7), ._5__2B(or_1_out), ._6__2Y(E2_07),
    ._7__GND(1'b0), ._14__Vcc(1'b1), ._13__4B(or_1_out), ._12__4A(B6), ._11__4Y(E2_06), ._10__3B(or_1_out),
    ._9__3A(B5), ._8__3Y(E2_05));
  _7486 u_7486_6 (
    ._1__1A(B4), ._2__1B(or_1_out), ._3__1Y(E2_04), ._4__2A(B3), ._5__2B(or_1_out), ._6__2Y(E2_03),
    ._7__GND(1'b0), ._14__Vcc(1'b1), ._13__4B(B2), ._12__4A(or_1_out), ._11__4Y(E2_02), ._10__3B(B1),
    ._9__3A(or_1_out), ._8__3Y(E2_01));
endmodule

// SMALL ALU
module SMALL_ALU (
  input  A12,
  input  A11,
  input  A10,
  input  A9,
  input  A8,
  input  A7,
  input  A6,
  input  A5,
  input  A4,
  input  A3,
  input  A2,
  input  A1,
  input  B12,
  input  B11,
  input  B10,
  input  B9,
  input  B8,
  input  B7,
  input  B6,
  input  B5,
  input  B4,
  input  B3,
  input  B2,
  input  B1,
  output V,
  output D12,
  output D11,
  output D10,
  output D09,
  output D08,
  output D07,
  output D06,
  output D05,
  output D04,
  output D03,
  output D02,
  output D01
);

  wire small_alu_prestep_1_e1_01, small_alu_prestep_1_e1_02, small_alu_prestep_1_e1_03,
       small_alu_prestep_1_e1_04, small_alu_prestep_1_e1_05, small_alu_prestep_1_e1_06,
       small_alu_prestep_1_e1_07, small_alu_prestep_1_e1_08, small_alu_prestep_1_e1_09,
       small_alu_prestep_1_e1_10, small_alu_prestep_1_e1_11, small_alu_prestep_1_e1_12,
       small_alu_prestep_1_e2_01, small_alu_prestep_1_e2_02, small_alu_prestep_1_e2_03,
       small_alu_prestep_1_e2_04, small_alu_prestep_1_e2_05, small_alu_prestep_1_e2_06,
       small_alu_prestep_1_e2_07, small_alu_prestep_1_e2_08, small_alu_prestep_1_e2_09,
       small_alu_prestep_1_e2_10, small_alu_prestep_1_e2_11, small_alu_prestep_1_e2_12;

  SMALL_ALU_prestep small_alu_prestep_1 (
    .A12(A12), .A11(A11), .A10(A10), .A9(A9), .A8(A8), .A7(A7), .A6(A6), .A5(A5), .A4(A4), .A3(A3), .A2(A2),
    .A1(A1), .B12(B12), .B11(B11), .B10(B10), .B9(B9), .B8(B8), .B7(B7), .B6(B6), .B5(B5), .B4(B4), .B3(B3),
    .B2(B2), .B1(B1), .E1_12(small_alu_prestep_1_e1_12), .E1_11(small_alu_prestep_1_e1_11),
    .E1_10(small_alu_prestep_1_e1_10), .E1_09(small_alu_prestep_1_e1_09), .E1_08(small_alu_prestep_1_e1_08),
    .E1_07(small_alu_prestep_1_e1_07), .E1_06(small_alu_prestep_1_e1_06), .E1_05(small_alu_prestep_1_e1_05),
    .E1_04(small_alu_prestep_1_e1_04), .E1_03(small_alu_prestep_1_e1_03), .E1_02(small_alu_prestep_1_e1_02),
    .E1_01(small_alu_prestep_1_e1_01), .E2_12(small_alu_prestep_1_e2_12), .E2_11(small_alu_prestep_1_e2_11),
    .E2_10(small_alu_prestep_1_e2_10), .E2_09(small_alu_prestep_1_e2_09), .E2_08(small_alu_prestep_1_e2_08),
    .E2_07(small_alu_prestep_1_e2_07), .E2_06(small_alu_prestep_1_e2_06), .E2_05(small_alu_prestep_1_e2_05),
    .E2_04(small_alu_prestep_1_e2_04), .E2_03(small_alu_prestep_1_e2_03), .E2_02(small_alu_prestep_1_e2_02),
    .E2_01(small_alu_prestep_1_e2_01));
  _12_bit_adder u_12_bit_adder_1 (
    .Cin(1'b1), .A12(small_alu_prestep_1_e1_12), .A11(small_alu_prestep_1_e1_11),
    .A10(small_alu_prestep_1_e1_10), .A9(small_alu_prestep_1_e1_09), .A8(small_alu_prestep_1_e1_08),
    .A7(small_alu_prestep_1_e1_07), .A6(small_alu_prestep_1_e1_06), .A5(small_alu_prestep_1_e1_05),
    .A4(small_alu_prestep_1_e1_04), .A3(small_alu_prestep_1_e1_03), .A2(small_alu_prestep_1_e1_02),
    .A1(small_alu_prestep_1_e1_01), .B12(small_alu_prestep_1_e2_12), .B11(small_alu_prestep_1_e2_11),
    .B10(small_alu_prestep_1_e2_10), .B9(small_alu_prestep_1_e2_09), .B8(small_alu_prestep_1_e2_08),
    .B7(small_alu_prestep_1_e2_07), .B6(small_alu_prestep_1_e2_06), .B5(small_alu_prestep_1_e2_05),
    .B4(small_alu_prestep_1_e2_04), .B3(small_alu_prestep_1_e2_03), .B2(small_alu_prestep_1_e2_02),
    .B1(small_alu_prestep_1_e2_01), .C_Bit(V), .S12(D12), .S11(D11), .S10(D10), .S9(D09), .S8(D08), .S7(D07),
    .S6(D06), .S5(D05), .S4(D04), .S3(D03), .S2(D02), .S1(D01));
endmodule
