// Logisim project MAIN_CIRCUIT.circ as structural Verilog: 16 circuits, main circuit main
module main (
  input  [31:0] in_1,
  input  [31:0] in_2,
  output [31:0] out_3
);

  TESTDRIVER testdriver_1 (
    .S1(in_1[31]), .E1_12_bits(in_1[30:19]), .F1_19_bits(in_1[18:0]), .S2(in_2[31]),
    .E2_12_bits(in_2[30:19]), .F2_19_bits(in_2[18:0]), .S(out_3[31]), .E(out_3[30:19]), .F(out_3[18:0]));
endmodule

module EXPONENT_SELECTOR (
  input  [11:0] E1,
  input  [11:0] E2,
  output GE12,
  output GE11,
  output GE10,
  output GE09,
  output GE08,
  output GE07,
  output GE06,
  output GE05,
  output GE04,
  output GE03,
  output GE02,
  output GE01,
  output A_B,
  output A_B_2,
  output A_B_3
);

  _12_bit_Comparator u_12_bit_comparator_1 (
    .A12(E1[11]), .A11(E1[10]), .A10(E1[9]), .A9(E1[8]), .A8(E1[7]), .A7(E1[6]), .A6(E1[5]), .A5(E1[4]),
    .A4(E1[3]), .A3(E1[2]), .A2(E1[1]), .A1(E1[0]), .B12(E2[11]), .B11(E2[10]), .B10(E2[9]), .B9(E2[8]),
    .B8(E2[7]), .B7(E2[6]), .B6(E2[5]), .B5(E2[4]), .B4(E2[3]), .B3(E2[2]), .B2(E2[1]), .B1(E2[0]),
    .A_B(A_B), .A_B_2(A_B_2), .A_B_3(A_B_3));
  _74157 u_74157_1 (
    ._1__S(A_B), ._2__A1(E2[7]), ._3__B1(E1[7]), ._4__Y1(GE08), ._5__A2(E2[6]), ._6__B2(E1[6]),
    ._7__Y2(GE07), ._8__GND(1'b0), ._16__Vcc(1'b1), ._15__G(1'b0), ._14__A4(E2[5]), ._13__B4(E1[5]),
    ._12__Y4(GE06), ._11__A3(E2[4]), ._10__B3(E1[4]), ._9__Y3(GE05));
  _74157 u_74157_2 (
    ._1__S(A_B), ._2__A1(E2[11]), ._3__B1(E1[11]), ._4__Y1(GE12), ._5__A2(E2[10]), ._6__B2(E1[10]),
    ._7__Y2(GE11), ._8__GND(1'b0), ._16__Vcc(1'b1), ._15__G(1'b0), ._14__A4(E2[9]), ._13__B4(E1[9]),
    ._12__Y4(GE10), ._11__A3(E2[8]), ._10__B3(E1[8]), ._9__Y3(GE09));
  _74157 u_74157_3 (
    ._1__S(A_B), ._2__A1(E2[3]), ._3__B1(E1[3]), ._4__Y1(GE04), ._5__A2(E2[2]), ._6__B2(E1[2]),
    ._7__Y2(GE03), ._8__GND(1'b0), ._16__Vcc(1'b1), ._15__G(1'b0), ._14__A4(E2[1]), ._13__B4(E1[1]),
    ._12__Y4(GE02), ._11__A3(E2[0]), ._10__B3(E1[0]), ._9__Y3(GE01));
endmodule

module FLOAT_SELECTOR (
  input  [18:0] F1,
  input  I_A_B,
  input  [18:0] F2,
  input  S1,
  input  S2,
  output out_6,
  output out_7,
  output out_8,
  output out_9,
  output out_10,
  output out_11,
  output out_12,
  output out_13,
  output out_14,
  output out_15,
  output out_16,
  output out_17,
  output out_18,
  output out_19,
  output out_20,
  output out_21,
  output out_22,
  output out_23,
  output out_24,
  output out_25
);

  _74157 u_74157_1 (
    ._1__S(I_A_B), ._2__A1(F1[4]), ._3__B1(F2[4]), ._4__Y1(out_21), ._5__A2(F1[3]), ._6__B2(F2[3]),
    ._7__Y2(out_22), ._16__Vcc(1'b1), ._15__G(1'b0), ._14__A4(F1[6]), ._13__B4(F2[6]), ._12__Y4(out_19),
    ._11__A3(F1[5]), ._10__B3(F2[5]), ._9__Y3(out_20));  // open: _8__GND
  _74157 u_74157_2 (
    ._1__S(I_A_B), ._2__A1(F1[1]), ._3__B1(F2[1]), ._4__Y1(out_24), ._5__A2(F1[0]), ._6__B2(F2[0]),
    ._7__Y2(out_25), ._8__GND(1'b0), ._16__Vcc(1'b1), ._15__G(1'b0), ._14__A4(F1[2]), ._13__B4(F2[2]),
    ._12__Y4(out_23), ._11__A3(S1), ._10__B3(S2), ._9__Y3(out_6));
  _74157 u_74157_3 (
    ._1__S(I_A_B), ._2__A1(F1[12]), ._3__B1(F2[12]), ._4__Y1(out_13), ._5__A2(F1[11]), ._6__B2(F2[11]),
    ._7__Y2(out_14), ._8__GND(1'b0), ._16__Vcc(1'b1), ._15__G(1'b0), ._14__A4(F1[14]), ._13__B4(F2[14]),
    ._12__Y4(out_11), ._11__A3(F1[13]), ._10__B3(F2[13]), ._9__Y3(out_12));
  _74157 u_74157_4 (
    ._1__S(I_A_B), ._2__A1(F1[9]), ._3__B1(F2[9]), ._4__Y1(out_16), ._5__A2(F1[7]), ._6__B2(F2[7]),
    ._7__Y2(out_18), ._8__GND(1'b0), ._16__Vcc(1'b1), ._15__G(1'b0), ._14__A4(F1[10]), ._13__B4(F2[10]),
    ._12__Y4(out_15), ._11__A3(F1[8]), ._10__B3(F2[8]), ._9__Y3(out_17));
  _74157 u_74157_5 (
    ._1__S(I_A_B), ._2__A1(F1[16]), ._3__B1(F2[16]), ._4__Y1(out_9), ._5__A2(F1[15]), ._6__B2(F2[15]),
    ._7__Y2(out_10), ._8__GND(1'b0), ._16__Vcc(1'b1), ._15__G(1'b0), ._14__A4(F1[18]), ._13__B4(F2[18]),
    ._12__Y4(out_7), ._11__A3(F1[17]), ._10__B3(F2[17]), ._9__Y3(out_8));
endmodule

module TESTDRIVER (
  input  S1,
  input  [11:0] E1_12_bits,
  input  [18:0] F1_19_bits,
  input  [11:0] E2_12_bits,
  input  [18:0] F2_19_bits,
  input  S2,
  output S,
  output [11:0] E,
  output [18:0] F
);

  wire big_alu_1_c, big_alu_1_o1, big_alu_1_o2, big_alu_1_o3, big_alu_1_o4, big_alu_1_o5, big_alu_1_o6,
       big_alu_1_o7, big_alu_1_o8, big_alu_1_o9, big_alu_1_o10, big_alu_1_o11, big_alu_1_o12, big_alu_1_o13,
       big_alu_1_o14, big_alu_1_o15, big_alu_1_o16, big_alu_1_o17, big_alu_1_o18, big_alu_1_o19,
       big_alu_1_o20, big_alu_1_o21, big_alu_1_o22, big_alu_1_o23, big_alu_1_o24, big_alu_1_o25,
       big_alu_1_o26, big_alu_1_o27, big_alu_1_o28, big_alu_1_o29, big_alu_1_o30, big_alu_1_o31,
       big_alu_1_o32, exponent_selector_1_a_b, float_selector_1_out_6, float_selector_1_out_7,
       float_selector_1_out_8, float_selector_1_out_9, float_selector_1_out_10, float_selector_1_out_11,
       float_selector_1_out_12, float_selector_1_out_13, float_selector_1_out_14, float_selector_1_out_15,
       float_selector_1_out_16, float_selector_1_out_17, float_selector_1_out_18, float_selector_1_out_19,
       float_selector_1_out_20, float_selector_1_out_21, float_selector_1_out_22, float_selector_1_out_23,
       float_selector_1_out_24, float_selector_1_out_25, float_selector_2_out_6, float_selector_2_out_7,
       float_selector_2_out_8, float_selector_2_out_9, float_selector_2_out_10, float_selector_2_out_11,
       float_selector_2_out_12, float_selector_2_out_13, float_selector_2_out_14, float_selector_2_out_15,
       float_selector_2_out_16, float_selector_2_out_17, float_selector_2_out_18, float_selector_2_out_19,
       float_selector_2_out_20, float_selector_2_out_21, float_selector_2_out_22, float_selector_2_out_23,
       float_selector_2_out_24, float_selector_2_out_25, n4_bit_add_1_or_0_1_cout, n12_bit_add_1_or_0_1_c,
       rounder_1_carry, rounder_1_integer, rounder_1_m0, rounder_1_m1, rounder_1_m2, rounder_1_m3,
       rounder_1_m4, rounder_1_m5, rounder_1_m6, rounder_1_m7, rounder_1_m8, rounder_1_m9, rounder_1_m10,
       rounder_1_m11, rounder_1_m12, rounder_1_m13, rounder_1_m14, rounder_1_m15, rounder_1_m16,
       rounder_1_m17, rounder_1_m18, rounder_1_out_5, shifter_1_o13, shifter_1_o14, shifter_1_o15,
       shifter_1_o16, shifter_1_o17, shifter_1_o18, shifter_1_o19, shifter_1_o20, shifter_1_o21,
       shifter_1_o22, shifter_1_o23, shifter_1_o24, shifter_1_o25, shifter_1_o26, shifter_1_o27,
       shifter_1_o28, shifter_1_o29, shifter_1_o30, shifter_1_o31, shifter_1_o32;
  wire [3:3] n4_bit_add_1_or_0_1_s4;
  wire [11:0] exponent_selector_1_ge01, normalizer_1_out_47, shifter_1_o1, small_alu_1_d12;
  wire [31:0] n32_bit_right_shifter_1_out_34, normalizer_1_out_46;

  SMALL_ALU small_alu_1 (
    .A12(E1_12_bits[11]), .A11(E1_12_bits[10]), .A10(E1_12_bits[9]), .A9(E1_12_bits[8]), .A8(E1_12_bits[7]),
    .A7(E1_12_bits[6]), .A6(E1_12_bits[5]), .A5(E1_12_bits[4]), .A4(E1_12_bits[3]), .A3(E1_12_bits[2]),
    .A2(E1_12_bits[1]), .A1(E1_12_bits[0]), .B12(E2_12_bits[11]), .B11(E2_12_bits[10]), .B10(E2_12_bits[9]),
    .B9(E2_12_bits[8]), .B8(E2_12_bits[7]), .B7(E2_12_bits[6]), .B6(E2_12_bits[5]), .B5(E2_12_bits[4]),
    .B4(E2_12_bits[3]), .B3(E2_12_bits[2]), .B2(E2_12_bits[1]), .B1(E2_12_bits[0]), .D12(small_alu_1_d12[0]),
    .D11(small_alu_1_d12[1]), .D10(small_alu_1_d12[2]), .D09(small_alu_1_d12[3]), .D08(small_alu_1_d12[4]),
    .D07(small_alu_1_d12[5]), .D06(small_alu_1_d12[6]), .D05(small_alu_1_d12[7]), .D04(small_alu_1_d12[8]),
    .D03(small_alu_1_d12[9]), .D02(small_alu_1_d12[10]), .D01(small_alu_1_d12[11]));  // open: V
  Rounder rounder_1 (
    .in_1(normalizer_1_out_46), .in_2(n32_bit_right_shifter_1_out_34[10]),
    .in_3(n32_bit_right_shifter_1_out_34[11]), .in_4(normalizer_1_out_47), .out_5(rounder_1_out_5),
    .out_15(E), .Carry(rounder_1_carry), .Integer(rounder_1_integer), .M0(rounder_1_m0), .M1(rounder_1_m1),
    .M2(rounder_1_m2), .M3(rounder_1_m3), .M4(rounder_1_m4), .M5(rounder_1_m5), .M6(rounder_1_m6),
    .M7(rounder_1_m7), .M8(rounder_1_m8), .M9(rounder_1_m9), .M10(rounder_1_m10), .M11(rounder_1_m11),
    .M12(rounder_1_m12), .M13(rounder_1_m13), .M14(rounder_1_m14), .M15(rounder_1_m15), .M16(rounder_1_m16),
    .M17(rounder_1_m17), .M18(rounder_1_m18));
  EXPONENT_SELECTOR exponent_selector_1 (
    .E1(E1_12_bits), .E2(E2_12_bits), .GE12(exponent_selector_1_ge01[11]),
    .GE11(exponent_selector_1_ge01[10]), .GE10(exponent_selector_1_ge01[9]),
    .GE09(exponent_selector_1_ge01[8]), .GE08(exponent_selector_1_ge01[7]),
    .GE07(exponent_selector_1_ge01[6]), .GE06(exponent_selector_1_ge01[5]),
    .GE05(exponent_selector_1_ge01[4]), .GE04(exponent_selector_1_ge01[3]),
    .GE03(exponent_selector_1_ge01[2]), .GE02(exponent_selector_1_ge01[1]),
    .GE01(exponent_selector_1_ge01[0]), .A_B(exponent_selector_1_a_b));  // open: A_B_2, A_B_3
  _32_Bit__Right_Shifter u_32_bit_right_shifter_1 (
    .OV(rounder_1_carry), .F32(rounder_1_carry), .F31(rounder_1_integer), .F30(rounder_1_m0),
    .F29(rounder_1_m1), .F28(rounder_1_m2), .F27(rounder_1_m3), .F26(rounder_1_m4), .F25(rounder_1_m5),
    .F24(rounder_1_m6), .F23(rounder_1_m7), .F22(rounder_1_m8), .F21(rounder_1_m9), .F20(rounder_1_m10),
    .F19(rounder_1_m11), .F18(rounder_1_m12), .F17(rounder_1_m13), .F16(rounder_1_m14), .F15(rounder_1_m15),
    .F14(rounder_1_m16), .F13(rounder_1_m17), .F12(rounder_1_m18), .F11(1'b0), .F10(1'b0), .F9(1'b0),
    .F8(1'b0), .F7(1'b0), .F6(1'b0), .F5(1'b0), .F4(1'b0), .F3(1'b0), .F2(1'b0), .F1(1'b0),
    .out_34(n32_bit_right_shifter_1_out_34));
  _4_bit_add_1_or_0 u_4_bit_add_1_or_0_1 (
    .A4(1'b0), .A3(n32_bit_right_shifter_1_out_34[29]), .A2(n32_bit_right_shifter_1_out_34[28]),
    .A1(n32_bit_right_shifter_1_out_34[27]), .Cout(n4_bit_add_1_or_0_1_cout), .S4(n4_bit_add_1_or_0_1_s4[3]),
    .S3(F[18]), .S2(F[17]), .S1(F[16]), .Cin(n12_bit_add_1_or_0_1_c));
  _4_bit_add_1_or_0 u_4_bit_add_1_or_0_2 (
    .A4(n32_bit_right_shifter_1_out_34[26]), .A3(n32_bit_right_shifter_1_out_34[25]),
    .A2(n32_bit_right_shifter_1_out_34[24]), .A1(n32_bit_right_shifter_1_out_34[23]), .S4(F[15]), .S3(F[14]),
    .S2(F[13]), .S1(F[12]), .Cin(n4_bit_add_1_or_0_1_cout));  // open: Cout
  _12_bit_add_1_or_0 u_12_bit_add_1_or_0_1 (
    .OV(rounder_1_out_5), .A12(n32_bit_right_shifter_1_out_34[22]), .A11(n32_bit_right_shifter_1_out_34[21]),
    .A10(n32_bit_right_shifter_1_out_34[20]), .A9(n32_bit_right_shifter_1_out_34[19]),
    .A8(n32_bit_right_shifter_1_out_34[18]), .A7(n32_bit_right_shifter_1_out_34[17]),
    .A6(n32_bit_right_shifter_1_out_34[16]), .A5(n32_bit_right_shifter_1_out_34[15]),
    .A4(n32_bit_right_shifter_1_out_34[14]), .A3(n32_bit_right_shifter_1_out_34[13]),
    .A2(n32_bit_right_shifter_1_out_34[12]), .A1(n32_bit_right_shifter_1_out_34[11]), .E12(F[11]),
    .E11(F[10]), .E10(F[9]), .E09(F[8]), .E08(F[7]), .E07(F[6]), .E06(F[5]), .E05(F[4]), .E04(F[3]),
    .E03(F[2]), .E02(F[1]), .E01(F[0]), .C(n12_bit_add_1_or_0_1_c));
  FLOAT_SELECTOR float_selector_1 (
    .I_A_B(exponent_selector_1_a_b), .S1(S1), .S2(S2), .F1(F1_19_bits), .F2(F2_19_bits),
    .out_6(float_selector_1_out_6), .out_7(float_selector_1_out_7), .out_8(float_selector_1_out_8),
    .out_9(float_selector_1_out_9), .out_10(float_selector_1_out_10), .out_11(float_selector_1_out_11),
    .out_12(float_selector_1_out_12), .out_13(float_selector_1_out_13), .out_14(float_selector_1_out_14),
    .out_15(float_selector_1_out_15), .out_16(float_selector_1_out_16), .out_17(float_selector_1_out_17),
    .out_18(float_selector_1_out_18), .out_19(float_selector_1_out_19), .out_20(float_selector_1_out_20),
    .out_21(float_selector_1_out_21), .out_22(float_selector_1_out_22), .out_23(float_selector_1_out_23),
    .out_24(float_selector_1_out_24), .out_25(float_selector_1_out_25));
  FLOAT_SELECTOR float_selector_2 (
    .I_A_B(exponent_selector_1_a_b), .S1(S2), .S2(S1), .F1(F2_19_bits), .F2(F1_19_bits),
    .out_6(float_selector_2_out_6), .out_7(float_selector_2_out_7), .out_8(float_selector_2_out_8),
    .out_9(float_selector_2_out_9), .out_10(float_selector_2_out_10), .out_11(float_selector_2_out_11),
    .out_12(float_selector_2_out_12), .out_13(float_selector_2_out_13), .out_14(float_selector_2_out_14),
    .out_15(float_selector_2_out_15), .out_16(float_selector_2_out_16), .out_17(float_selector_2_out_17),
    .out_18(float_selector_2_out_18), .out_19(float_selector_2_out_19), .out_20(float_selector_2_out_20),
    .out_21(float_selector_2_out_21), .out_22(float_selector_2_out_22), .out_23(float_selector_2_out_23),
    .out_24(float_selector_2_out_24), .out_25(float_selector_2_out_25));
  SHIFTER shifter_1 (
    .F19(float_selector_1_out_7), .F18(float_selector_1_out_8), .F17(float_selector_1_out_9),
    .F16(float_selector_1_out_10), .F15(float_selector_1_out_11), .F14(float_selector_1_out_12),
    .F13(float_selector_1_out_13), .F12(float_selector_1_out_14), .F11(float_selector_1_out_15),
    .F10(float_selector_1_out_16), .F9(float_selector_1_out_17), .F8(float_selector_1_out_18),
    .F7(float_selector_1_out_19), .F6(float_selector_1_out_20), .F5(float_selector_1_out_21),
    .F4(float_selector_1_out_22), .F3(float_selector_1_out_23), .F2(float_selector_1_out_24),
    .F1(float_selector_1_out_25), .E12(small_alu_1_d12[0]), .E11(small_alu_1_d12[1]),
    .E10(small_alu_1_d12[2]), .E09(small_alu_1_d12[3]), .E08(small_alu_1_d12[4]), .E07(small_alu_1_d12[5]),
    .E06(small_alu_1_d12[6]), .E05(small_alu_1_d12[7]), .E04(small_alu_1_d12[8]), .E03(small_alu_1_d12[9]),
    .E02(small_alu_1_d12[10]), .E01(small_alu_1_d12[11]), .O32(shifter_1_o32), .O31(shifter_1_o31),
    .O30(shifter_1_o30), .O29(shifter_1_o29), .O28(shifter_1_o28), .O27(shifter_1_o27), .O26(shifter_1_o26),
    .O25(shifter_1_o25), .O24(shifter_1_o24), .O23(shifter_1_o23), .O22(shifter_1_o22), .O21(shifter_1_o21),
    .O20(shifter_1_o20), .O19(shifter_1_o19), .O18(shifter_1_o18), .O17(shifter_1_o17), .O16(shifter_1_o16),
    .O15(shifter_1_o15), .O14(shifter_1_o14), .O13(shifter_1_o13), .O12(shifter_1_o1[11]),
    .O11(shifter_1_o1[10]), .O10(shifter_1_o1[9]), .O9(shifter_1_o1[8]), .O8(shifter_1_o1[7]),
    .O7(shifter_1_o1[6]), .O6(shifter_1_o1[5]), .O5(shifter_1_o1[4]), .O4(shifter_1_o1[3]),
    .O3(shifter_1_o1[2]), .O2(shifter_1_o1[1]), .O1(shifter_1_o1[0]));
  BIG_ALU big_alu_1 (
    .SA(float_selector_1_out_6), .A32(shifter_1_o32), .A31(shifter_1_o31), .A30(shifter_1_o30),
    .A29(shifter_1_o29), .A28(shifter_1_o28), .A27(shifter_1_o27), .A26(shifter_1_o26), .A25(shifter_1_o25),
    .A24(shifter_1_o24), .A23(shifter_1_o23), .A22(shifter_1_o22), .A21(shifter_1_o21), .A20(shifter_1_o20),
    .A19(shifter_1_o19), .A18(shifter_1_o18), .A17(shifter_1_o17), .A16(shifter_1_o16), .A15(shifter_1_o15),
    .A14(shifter_1_o14), .A13(shifter_1_o13), .SB(float_selector_2_out_6), .B32(1'b1),
    .B31(float_selector_2_out_7), .B30(float_selector_2_out_8), .B29(float_selector_2_out_9),
    .B28(float_selector_2_out_10), .B27(float_selector_2_out_11), .B26(float_selector_2_out_12),
    .B25(float_selector_2_out_13), .B24(float_selector_2_out_14), .B23(float_selector_2_out_15),
    .B22(float_selector_2_out_16), .B21(float_selector_2_out_17), .B20(float_selector_2_out_18),
    .B19(float_selector_2_out_19), .B18(float_selector_2_out_20), .B17(float_selector_2_out_21),
    .B16(float_selector_2_out_22), .B15(float_selector_2_out_23), .B14(float_selector_2_out_24),
    .B13(float_selector_2_out_25), .A12(shifter_1_o1[11]), .A11(shifter_1_o1[10]), .A10(shifter_1_o1[9]),
    .A9(shifter_1_o1[8]), .A8(shifter_1_o1[7]), .A7(shifter_1_o1[6]), .A6(shifter_1_o1[5]),
    .A5(shifter_1_o1[4]), .A4(shifter_1_o1[3]), .A3(shifter_1_o1[2]), .A2(shifter_1_o1[1]),
    .A1(shifter_1_o1[0]), .B12(1'b0), .B11(1'b0), .B10(1'b0), .B9(1'b0), .B8(1'b0), .B7(1'b0), .B6(1'b0),
    .B5(1'b0), .B4(1'b0), .B3(1'b0), .B2(1'b0), .B1(1'b0), .C(big_alu_1_c), .S(S), .O32(big_alu_1_o32),
    .O31(big_alu_1_o31), .O30(big_alu_1_o30), .O29(big_alu_1_o29), .O28(big_alu_1_o28), .O27(big_alu_1_o27),
    .O26(big_alu_1_o26), .O25(big_alu_1_o25), .O24(big_alu_1_o24), .O23(big_alu_1_o23), .O22(big_alu_1_o22),
    .O21(big_alu_1_o21), .O20(big_alu_1_o20), .O19(big_alu_1_o19), .O18(big_alu_1_o18), .O17(big_alu_1_o17),
    .O16(big_alu_1_o16), .O15(big_alu_1_o15), .O14(big_alu_1_o14), .O13(big_alu_1_o13), .O12(big_alu_1_o12),
    .O11(big_alu_1_o11), .O10(big_alu_1_o10), .O9(big_alu_1_o9), .O8(big_alu_1_o8), .O7(big_alu_1_o7),
    .O6(big_alu_1_o6), .O5(big_alu_1_o5), .O4(big_alu_1_o4), .O3(big_alu_1_o3), .O2(big_alu_1_o2),
    .O1(big_alu_1_o1));  // open: OV
  NORMALIZER normalizer_1 (
    .OV(big_alu_1_c), .F32(big_alu_1_o32), .F31(big_alu_1_o31), .F30(big_alu_1_o30), .F29(big_alu_1_o29),
    .F28(big_alu_1_o28), .F27(big_alu_1_o27), .F26(big_alu_1_o26), .F25(big_alu_1_o25), .F24(big_alu_1_o24),
    .F23(big_alu_1_o23), .F22(big_alu_1_o22), .F21(big_alu_1_o21), .F20(big_alu_1_o20), .F19(big_alu_1_o19),
    .F18(big_alu_1_o18), .F17(big_alu_1_o17), .F16(big_alu_1_o16), .F15(big_alu_1_o15), .F14(big_alu_1_o14),
    .F13(big_alu_1_o13), .F12(big_alu_1_o12), .F11(big_alu_1_o11), .F10(big_alu_1_o10), .F9(big_alu_1_o9),
    .F8(big_alu_1_o8), .F7(big_alu_1_o7), .F6(big_alu_1_o6), .F5(big_alu_1_o5), .F4(big_alu_1_o4),
    .F3(big_alu_1_o3), .F2(big_alu_1_o2), .F1(big_alu_1_o1), .A12(exponent_selector_1_ge01[11]),
    .A11(exponent_selector_1_ge01[10]), .A10(exponent_selector_1_ge01[9]), .A9(exponent_selector_1_ge01[8]),
    .A8(exponent_selector_1_ge01[7]), .A7(exponent_selector_1_ge01[6]), .A6(exponent_selector_1_ge01[5]),
    .A5(exponent_selector_1_ge01[4]), .A4(exponent_selector_1_ge01[3]), .A3(exponent_selector_1_ge01[2]),
    .A2(exponent_selector_1_ge01[1]), .A1(exponent_selector_1_ge01[0]), .out_47(normalizer_1_out_47),
    .out_46(normalizer_1_out_46));
endmodule

// RS
module _32_Bit__Right_Shifter (
  input  OV,
  input  F32,
  input  F31,
  input  F30,
  input  F29,
  input  F28,
  input  F27,
  input  F26,
  input  F25,
  input  F24,
  input  F23,
  input  F22,
  input  F21,
  input  F20,
  input  F19,
  input  F18,
  input  F17,
  input  F16,
  input  F15,
  input  F14,
  input  F13,
  input  F12,
  input  F11,
  input  F10,
  input  F9,
  input  F8,
  input  F7,
  input  F6,
  input  F5,
  input  F4,
  input  F3,
  input  F2,
  input  F1,
  output [31:0] out_34
);

  Shifter #(.width(32), .shift("rr")) shifter_1 (
    .in({F32, F31, F30, F29, F28, F27, F26, F25, F24, F23, F22, F21, F20, F19, F18, F17, F16, F15, F14, F13, F12, F11, F10, F9, F8, F7, F6, F5, F4, F3, F2, F1}),
    .\dist ({4'b0000, OV}), .out(out_34));
endmodule

// LS
module _32_Bit_Left_Shifter (
  input  [4:0] in_1,
  input  F32,
  input  F31,
  input  F30,
  input  F29,
  input  F28,
  input  F27,
  input  F26,
  input  F25,
  input  F24,
  input  F23,
  input  F22,
  input  F21,
  input  F20,
  input  F19,
  input  F18,
  input  F17,
  input  F16,
  input  F15,
  input  F14,
  input  F13,
  input  F12,
  input  F11,
  input  F10,
  input  F9,
  input  F8,
  input  F7,
  input  F6,
  input  F5,
  input  F4,
  input  F3,
  input  F2,
  input  F1,
  output [31:0] out_34,
  output L_Bit
);

  Shifter #(.width(32)) shifter_1 (
    .in({F32, F31, F30, F29, F28, F27, F26, F25, F24, F23, F22, F21, F20, F19, F18, F17, F16, F15, F14, F13, F12, F11, F10, F9, F8, F7, F6, F5, F4, F3, F2, F1}),
    .\dist (in_1), .out({L_Bit, out_34[30:0]}));

  assign out_34[31] = L_Bit;
endmodule

// PRESTEP
module NORMALIZER_prestep (
  input  OV,
  input  F32,
  input  F31,
  input  F30,
  input  F29,
  input  F28,
  input  F27,
  input  F26,
  input  F25,
  input  F24,
  input  F23,
  input  F22,
  input  F21,
  input  F20,
  input  F19,
  input  F18,
  input  F17,
  input  F16,
  input  F15,
  input  F14,
  input  F13,
  input  F12,
  input  F11,
  input  F10,
  input  F9,
  input  F8,
  input  F7,
  input  F6,
  input  F5,
  input  F4,
  input  F3,
  input  F2,
  input  F1,
  output [4:0] P,
  output [31:0] F,
  output out_36,
  output [4:0] P_prime
);

  wire n7486_1__3__1y;
  wire [31:0] n32_bit_right_shifter_1_out_34;

  _7486 u_7486_1 (
    ._1__1A(OV), ._2__1B(F1), ._3__1Y(n7486_1__3__1y), ._7__GND(1'b0), ._14__Vcc(1'b1));  // open: _4__2A, _5__2B, _6__2Y, _13__4B, _12__4A, _11__4Y, _10__3B, _9__3A, _8__3Y
  _32_Bit__Right_Shifter u_32_bit_right_shifter_1 (
    .OV(OV), .F32(F32), .F31(F31), .F30(F30), .F29(F29), .F28(F28), .F27(F27), .F26(F26), .F25(F25),
    .F24(F24), .F23(F23), .F22(F22), .F21(F21), .F20(F20), .F19(F19), .F18(F18), .F17(F17), .F16(F16),
    .F15(F15), .F14(F14), .F13(F13), .F12(F12), .F11(F11), .F10(F10), .F9(F9), .F8(F8), .F7(F7), .F6(F6),
    .F5(F5), .F4(F4), .F3(F3), .F2(F2), .F1(n7486_1__3__1y), .out_34(n32_bit_right_shifter_1_out_34));
  _32_Bit_Left_Shifter u_32_bit_left_shifter_1 (
    .in_1(P), .F32(n32_bit_right_shifter_1_out_34[31]), .F31(n32_bit_right_shifter_1_out_34[30]),
    .F30(n32_bit_right_shifter_1_out_34[29]), .F29(n32_bit_right_shifter_1_out_34[28]),
    .F28(n32_bit_right_shifter_1_out_34[27]), .F27(n32_bit_right_shifter_1_out_34[26]),
    .F26(n32_bit_right_shifter_1_out_34[25]), .F25(n32_bit_right_shifter_1_out_34[24]),
    .F24(n32_bit_right_shifter_1_out_34[23]), .F23(n32_bit_right_shifter_1_out_34[22]),
    .F22(n32_bit_right_shifter_1_out_34[21]), .F21(n32_bit_right_shifter_1_out_34[20]),
    .F20(n32_bit_right_shifter_1_out_34[19]), .F19(n32_bit_right_shifter_1_out_34[18]),
    .F18(n32_bit_right_shifter_1_out_34[17]), .F17(n32_bit_right_shifter_1_out_34[16]),
    .F16(n32_bit_right_shifter_1_out_34[15]), .F15(n32_bit_right_shifter_1_out_34[14]),
    .F14(n32_bit_right_shifter_1_out_34[13]), .F13(n32_bit_right_shifter_1_out_34[12]),
    .F12(n32_bit_right_shifter_1_out_34[11]), .F11(n32_bit_right_shifter_1_out_34[10]),
    .F10(n32_bit_right_shifter_1_out_34[9]), .F9(n32_bit_right_shifter_1_out_34[8]),
    .F8(n32_bit_right_shifter_1_out_34[7]), .F7(n32_bit_right_shifter_1_out_34[6]),
    .F6(n32_bit_right_shifter_1_out_34[5]), .F5(n32_bit_right_shifter_1_out_34[4]),
    .F4(n32_bit_right_shifter_1_out_34[3]), .F3(n32_bit_right_shifter_1_out_34[2]),
    .F2(n32_bit_right_shifter_1_out_34[1]), .F1(n32_bit_right_shifter_1_out_34[0]), .out_34(F), .L_Bit(out_36));
  _32_5_priority_encoder u_32_5_priority_encoder_1 (
    .F32(n32_bit_right_shifter_1_out_34[31]), .F31(n32_bit_right_shifter_1_out_34[30]),
    .F30(n32_bit_right_shifter_1_out_34[29]), .F29(n32_bit_right_shifter_1_out_34[28]),
    .F28(n32_bit_right_shifter_1_out_34[27]), .F27(n32_bit_right_shifter_1_out_34[26]),
    .F26(n32_bit_right_shifter_1_out_34[25]), .F25(n32_bit_right_shifter_1_out_34[24]),
    .F24(n32_bit_right_shifter_1_out_34[23]), .F23(n32_bit_right_shifter_1_out_34[22]),
    .F22(n32_bit_right_shifter_1_out_34[21]), .F21(n32_bit_right_shifter_1_out_34[20]),
    .F20(n32_bit_right_shifter_1_out_34[19]), .F19(n32_bit_right_shifter_1_out_34[18]),
    .F18(n32_bit_right_shifter_1_out_34[17]), .F17(n32_bit_right_shifter_1_out_34[16]),
    .F16(n32_bit_right_shifter_1_out_34[15]), .F15(n32_bit_right_shifter_1_out_34[14]),
    .F14(n32_bit_right_shifter_1_out_34[13]), .F13(n32_bit_right_shifter_1_out_34[12]),
    .F12(n32_bit_right_shifter_1_out_34[11]), .F11(n32_bit_right_shifter_1_out_34[10]),
    .F10(n32_bit_right_shifter_1_out_34[9]), .F9(n32_bit_right_shifter_1_out_34[8]),
    .F8(n32_bit_right_shifter_1_out_34[7]), .F7(n32_bit_right_shifter_1_out_34[6]),
    .F6(n32_bit_right_shifter_1_out_34[5]), .F5(n32_bit_right_shifter_1_out_34[4]),
    .F4(n32_bit_right_shifter_1_out_34[3]), .F3(n32_bit_right_shifter_1_out_34[2]),
    .F2(n32_bit_right_shifter_1_out_34[1]), .F1(n32_bit_right_shifter_1_out_34[0]), .P5_prime(P_prime[4]),
    .P4_prime(P_prime[3]), .P3_prime(P_prime[2]), .P2_prime(P_prime[1]), .P1_prime(P_prime[0]), .P5(P[4]),
    .P4(P[3]), .P3(P[2]), .P2(P[1]), .P1(P[0]));
endmodule

// Priority Encoder
module _32_5_priority_encoder (
  input  F32,
  input  F31,
  input  F30,
  input  F29,
  input  F28,
  input  F27,
  input  F26,
  input  F25,
  input  F24,
  input  F23,
  input  F22,
  input  F21,
  input  F20,
  input  F19,
  input  F18,
  input  F17,
  input  F16,
  input  F15,
  input  F14,
  input  F13,
  input  F12,
  input  F11,
  input  F10,
  input  F9,
  input  F8,
  input  F7,
  input  F6,
  input  F5,
  input  F4,
  input  F3,
  input  F2,
  input  F1,
  output P5_prime,
  output P4_prime,
  output P3_prime,
  output P2_prime,
  output P1_prime,
  output P5,
  output P4,
  output P3,
  output P2,
  output P1
);

  wire n7404_1__8__4y, n7408_1__11__4y, n7432_1__3__1y, n7432_1__6__2y, n7432_1__11__4y, n74148_1__6__a2,
       n74148_1__7__a1, n74148_1__9__a0, n74148_1__14__ngs__nc, n74148_1__15__neo__nc, n74148_2__6__a2,
       n74148_2__7__a1, n74148_2__9__a0, n74148_2__14__ngs__nc, n74148_2__15__neo__nc, n74148_3__6__a2,
       n74148_3__7__a1, n74148_3__9__a0, n74148_3__14__ngs__nc, n74148_3__15__neo__nc, n74148_4__6__a2,
       n74148_4__7__a1, n74148_4__9__a0, n74148_4__15__neo__nc;

  _74148 u_74148_1 (
    ._1__I4(F29), ._2__I5(F30), ._3__I6(F31), ._4__I7(F32), ._5__nEI__NC(1'b0), ._6__A2(n74148_1__6__a2),
    ._7__A1(n74148_1__7__a1), ._8__GND(1'b0), ._16__Vcc(1'b1), ._15__nEO__NC(n74148_1__15__neo__nc),
    ._14__nGS__NC(n74148_1__14__ngs__nc), ._13__I3(F28), ._12__I2(F27), ._11__I1(F26), ._10__I0(F25),
    ._9__A0(n74148_1__9__a0));
  _74148 u_74148_2 (
    ._1__I4(F21), ._2__I5(F22), ._3__I6(F23), ._4__I7(F24), ._5__nEI__NC(n74148_1__15__neo__nc),
    ._6__A2(n74148_2__6__a2), ._7__A1(n74148_2__7__a1), ._8__GND(1'b0), ._16__Vcc(1'b1),
    ._15__nEO__NC(n74148_2__15__neo__nc), ._14__nGS__NC(n74148_2__14__ngs__nc), ._13__I3(F20), ._12__I2(F19),
    ._11__I1(F18), ._10__I0(F17), ._9__A0(n74148_2__9__a0));
  _74148 u_74148_3 (
    ._1__I4(F13), ._2__I5(F14), ._3__I6(F15), ._4__I7(F16), ._5__nEI__NC(n74148_2__15__neo__nc),
    ._6__A2(n74148_3__6__a2), ._7__A1(n74148_3__7__a1), ._8__GND(1'b0), ._16__Vcc(1'b1),
    ._15__nEO__NC(n74148_3__15__neo__nc), ._14__nGS__NC(n74148_3__14__ngs__nc), ._13__I3(F12), ._12__I2(F11),
    ._11__I1(F10), ._10__I0(F9), ._9__A0(n74148_3__9__a0));
  _74148 u_74148_4 (
    ._1__I4(F5), ._2__I5(F6), ._3__I6(F7), ._4__I7(F8), ._5__nEI__NC(n74148_3__15__neo__nc),
    ._6__A2(n74148_4__6__a2), ._7__A1(n74148_4__7__a1), ._8__GND(1'b0), ._16__Vcc(1'b1),
    ._15__nEO__NC(n74148_4__15__neo__nc), ._13__I3(F4), ._12__I2(F3), ._11__I1(F2), ._10__I0(F1),
    ._9__A0(n74148_4__9__a0));  // open: _14__nGS__NC
  _7432 u_7432_1 (
    ._1__1A(n7404_1__8__4y), ._2__1B(n74148_1__6__a2), ._3__1Y(n7432_1__3__1y), ._4__2A(n7404_1__8__4y),
    ._5__2B(n74148_1__7__a1), ._6__2Y(n7432_1__6__2y), ._7__GND(1'b0), ._14__Vcc(1'b1),
    ._13__4B(n7404_1__8__4y), ._12__4A(n74148_1__9__a0), ._11__4Y(n7432_1__11__4y));  // open: _10__3B, _9__3A, _8__3Y
  _7408 u_7408_1 (
    ._1__1A(n7408_1__11__4y), ._2__1B(n74148_2__14__ngs__nc), ._3__1Y(P5), ._4__2A(n7408_1__11__4y),
    ._5__2B(n74148_3__14__ngs__nc), ._6__2Y(P4), ._7__GND(1'b0), ._14__Vcc(1'b1),
    ._13__4B(n74148_4__15__neo__nc), ._12__4A(n74148_1__14__ngs__nc), ._11__4Y(n7408_1__11__4y));  // open: _10__3B, _9__3A, _8__3Y
  _74153 u_74153_1 (
    ._1__nG1(1'b0), ._2__B(P5), ._3__1C3(n74148_4__6__a2), ._4__1C2(n74148_3__6__a2),
    ._5__1C1(n74148_2__6__a2), ._6__1C0(n7432_1__3__1y), ._7__Y1(P3_prime), ._8__GND(1'b0), ._16__Vcc(1'b1),
    ._15__nG2(1'b0), ._14__A(P4), ._13__2C3(n74148_4__7__a1), ._12__2C2(n74148_3__7__a1),
    ._11__2C1(n74148_2__7__a1), ._10__2C0(n7432_1__6__2y), ._9__Y2(P2_prime));
  _74153 u_74153_2 (
    ._1__nG1(1'b0), ._2__B(P5), ._3__1C3(n74148_4__9__a0), ._4__1C2(n74148_3__9__a0),
    ._5__1C1(n74148_2__9__a0), ._6__1C0(n7432_1__11__4y), ._7__Y1(P1_prime), ._8__GND(1'b0), ._16__Vcc(1'b1),
    ._15__nG2(1'b0), ._14__A(P4));  // open: _13__2C3, _12__2C2, _11__2C1, _10__2C0, _9__Y2
  _7404 u_7404_1 (
    ._1__1A(P3_prime), ._2__1Y(P3), ._3__2A(P2_prime), ._4__2Y(P2), ._5__3A(P1_prime), ._6__3Y(P1),
    ._7__GND(1'b0), ._14__Vcc(1'b1), ._13__6A(P4), ._12__6Y(P4_prime), ._11__5A(P5), ._10__5Y(P5_prime),
    ._9__4A(n74148_4__15__neo__nc), ._8__4Y(n7404_1__8__4y));
endmodule

module NORMALIZER (
  input  OV,
  input  A12,
  input  A11,
  input  A10,
  input  A9,
  input  A8,
  input  A7,
  input  A6,
  input  A5,
  input  A4,
  input  A3,
  input  A2,
  input  A1,
  input  F32,
  input  F31,
  input  F30,
  input  F29,
  input  F28,
  input  F27,
  input  F26,
  input  F25,
  input  F24,
  input  F23,
  input  F22,
  input  F21,
  input  F20,
  input  F19,
  input  F18,
  input  F17,
  input  F16,
  input  F15,
  input  F14,
  input  F13,
  input  F12,
  input  F11,
  input  F10,
  input  F9,
  input  F8,
  input  F7,
  input  F6,
  input  F5,
  input  F4,
  input  F3,
  input  F2,
  input  F1,
  output [31:0] out_46,
  output [11:0] out_47
);

  wire n12_bit_1_bit_and_1_e01, n12_bit_1_bit_and_1_e02, n12_bit_1_bit_and_1_e03, n12_bit_1_bit_and_1_e04,
       n12_bit_1_bit_and_1_e05, n12_bit_1_bit_and_1_e06, n12_bit_1_bit_and_1_e07, n12_bit_1_bit_and_1_e08,
       n12_bit_1_bit_and_1_e09, n12_bit_1_bit_and_1_e10, n12_bit_1_bit_and_1_e11, n12_bit_1_bit_and_1_e12,
       n12_bit_add_1_or_0_1_e01, n12_bit_add_1_or_0_1_e02, n12_bit_add_1_or_0_1_e03,
       n12_bit_add_1_or_0_1_e04, n12_bit_add_1_or_0_1_e05, n12_bit_add_1_or_0_1_e06,
       n12_bit_add_1_or_0_1_e07, n12_bit_add_1_or_0_1_e08, n12_bit_add_1_or_0_1_e09,
       n12_bit_add_1_or_0_1_e10, n12_bit_add_1_or_0_1_e11, n12_bit_add_1_or_0_1_e12,
       normalizer_prestep_1_out_36;
  wire [4:0] normalizer_prestep_1_p_prime;

  NORMALIZER_prestep normalizer_prestep_1 (
    .OV(OV), .F32(F32), .F31(F31), .F30(F30), .F29(F29), .F28(F28), .F27(F27), .F26(F26), .F25(F25),
    .F24(F24), .F23(F23), .F22(F22), .F21(F21), .F20(F20), .F19(F19), .F18(F18), .F17(F17), .F16(F16),
    .F15(F15), .F14(F14), .F13(F13), .F12(F12), .F11(F11), .F10(F10), .F9(F9), .F8(F8), .F7(F7), .F6(F6),
    .F5(F5), .F4(F4), .F3(F3), .F2(F2), .F1(F1), .F(out_46), .out_36(normalizer_prestep_1_out_36),
    .P_prime(normalizer_prestep_1_p_prime));  // open: P
  _12_bit__1_bit_AND u_12_bit_1_bit_and_1 (
    .B(normalizer_prestep_1_out_36), .A12(n12_bit_add_1_or_0_1_e12), .A11(n12_bit_add_1_or_0_1_e11),
    .A10(n12_bit_add_1_or_0_1_e10), .A9(n12_bit_add_1_or_0_1_e09), .A8(n12_bit_add_1_or_0_1_e08),
    .A7(n12_bit_add_1_or_0_1_e07), .A6(n12_bit_add_1_or_0_1_e06), .A5(n12_bit_add_1_or_0_1_e05),
    .A4(n12_bit_add_1_or_0_1_e04), .A3(n12_bit_add_1_or_0_1_e03), .A2(n12_bit_add_1_or_0_1_e02),
    .A1(n12_bit_add_1_or_0_1_e01), .E12(n12_bit_1_bit_and_1_e12), .E11(n12_bit_1_bit_and_1_e11),
    .E10(n12_bit_1_bit_and_1_e10), .E09(n12_bit_1_bit_and_1_e09), .E08(n12_bit_1_bit_and_1_e08),
    .E07(n12_bit_1_bit_and_1_e07), .E06(n12_bit_1_bit_and_1_e06), .E05(n12_bit_1_bit_and_1_e05),
    .E04(n12_bit_1_bit_and_1_e04), .E03(n12_bit_1_bit_and_1_e03), .E02(n12_bit_1_bit_and_1_e02),
    .E01(n12_bit_1_bit_and_1_e01));
  _12_bit_add_1_or_0 u_12_bit_add_1_or_0_1 (
    .OV(OV), .A12(A12), .A11(A11), .A10(A10), .A9(A9), .A8(A8), .A7(A7), .A6(A6), .A5(A5), .A4(A4), .A3(A3),
    .A2(A2), .A1(A1), .E12(n12_bit_add_1_or_0_1_e12), .E11(n12_bit_add_1_or_0_1_e11),
    .E10(n12_bit_add_1_or_0_1_e10), .E09(n12_bit_add_1_or_0_1_e09), .E08(n12_bit_add_1_or_0_1_e08),
    .E07(n12_bit_add_1_or_0_1_e07), .E06(n12_bit_add_1_or_0_1_e06), .E05(n12_bit_add_1_or_0_1_e05),
    .E04(n12_bit_add_1_or_0_1_e04), .E03(n12_bit_add_1_or_0_1_e03), .E02(n12_bit_add_1_or_0_1_e02),
    .E01(n12_bit_add_1_or_0_1_e01));  // open: C
  Add_12_bit add_12_bit_1 (
    .A12(n12_bit_1_bit_and_1_e12), .A11(n12_bit_1_bit_and_1_e11), .A10(n12_bit_1_bit_and_1_e10),
    .A9(n12_bit_1_bit_and_1_e09), .A8(n12_bit_1_bit_and_1_e08), .A7(n12_bit_1_bit_and_1_e07),
    .A6(n12_bit_1_bit_and_1_e06), .A5(n12_bit_1_bit_and_1_e05), .A4(n12_bit_1_bit_and_1_e04),
    .A3(n12_bit_1_bit_and_1_e03), .A2(n12_bit_1_bit_and_1_e02), .A1(n12_bit_1_bit_and_1_e01), .B4(1'b1),
    .B3(1'b1), .B2(1'b1), .B1(1'b1), .B8(1'b1), .B7(1'b1), .B6(1'b1), .B5(normalizer_prestep_1_p_prime[4]),
    .B4_2(normalizer_prestep_1_p_prime[3]), .B3_2(normalizer_prestep_1_p_prime[2]),
    .B2_2(normalizer_prestep_1_p_prime[1]), .B1_2(normalizer_prestep_1_p_prime[0]), .S12(out_47[11]),
    .S11(out_47[10]), .S10(out_47[9]), .S9(out_47[8]), .S8(out_47[7]), .S7(out_47[6]), .S6(out_47[5]),
    .S5(out_47[4]), .S4(out_47[3]), .S3(out_47[2]), .S2(out_47[1]), .S1(out_47[0]), .Cin(1'b1));  // open: Cout
endmodule

// Add 1/0
module _4_bit_add_1_or_0 (
  input  A4,
  input  A3,
  input  A2,
  input  A1,
  input  Cin,
  output Cout,
  output S4,
  output S3,
  output S2,
  output S1
);

  _7483 u_7483_1 (
    ._1__A4(A4), ._2__S3(S3), ._3__A3(A3), ._4__B3(1'b0), ._5__Vcc(1'b1), ._6__S2(S2), ._7__B2(1'b0),
    ._8__A2(A2), ._16__B4(1'b0), ._15__S4(S4), ._14_Cout(Cout), ._13__Cin(Cin), ._12__GND(1'b0),
    ._11__B1(1'b0), ._10__A1(A1), ._9__S1(S1));
endmodule

// Add 1/0
module _12_bit_add_1_or_0 (
  input  A12,
  input  A11,
  input  A10,
  input  A9,
  input  A8,
  input  A7,
  input  A6,
  input  A5,
  input  A4,
  input  A3,
  input  A2,
  input  A1,
  input  OV,
  output C,
  output E12,
  output E11,
  output E10,
  output E09,
  output E08,
  output E07,
  output E06,
  output E05,
  output E04,
  output E03,
  output E02,
  output E01
);

  wire n4_bit_add_1_or_0_2_cout, n4_bit_add_1_or_0_3_cout;

  _4_bit_add_1_or_0 u_4_bit_add_1_or_0_1 (
    .A4(A12), .A3(A11), .A2(A10), .A1(A9), .Cout(C), .S4(E12), .S3(E11), .S2(E10), .S1(E09),
    .Cin(n4_bit_add_1_or_0_2_cout));
  _4_bit_add_1_or_0 u_4_bit_add_1_or_0_2 (
    .A4(A8), .A3(A7), .A2(A6), .A1(A5), .Cout(n4_bit_add_1_or_0_2_cout), .S4(E08), .S3(E07), .S2(E06),
    .S1(E05), .Cin(n4_bit_add_1_or_0_3_cout));
  _4_bit_add_1_or_0 u_4_bit_add_1_or_0_3 (
    .A4(A4), .A3(A3), .A2(A2), .A1(A1), .Cout(n4_bit_add_1_or_0_3_cout), .S4(E04), .S3(E03), .S2(E02),
    .S1(E01), .Cin(OV));
endmodule

// 12 Bit Adder
module Add_12_bit (
  input  A12,
  input  A11,
  input  A10,
  input  A9,
  input  A8,
  input  A7,
  input  A6,
  input  A5,
  input  A4,
  input  A3,
  input  A2,
  input  A1,
  input  B4,
  input  B3,
  input  B2,
  input  B1,
  input  B8,
  input  B7,
  input  B6,
  input  B5,
  input  B4_2,
  input  B3_2,
  input  B2_2,
  input  B1_2,
  input  Cin,
  output Cout,
  output S12,
  output S11,
  output S10,
  output S9,
  output S8,
  output S7,
  output S6,
  output S5,
  output S4,
  output S3,
  output S2,
  output S1
);

  wire n7483_2__14_cout, n7483_3__14_cout;

  _7483 u_7483_1 (
    ._1__A4(A12), ._2__S3(S11), ._3__A3(A11), ._4__B3(B3), ._5__Vcc(1'b1), ._6__S2(S10), ._7__B2(B2),
    ._8__A2(A10), ._16__B4(B4), ._15__S4(S12), ._14_Cout(Cout), ._13__Cin(n7483_2__14_cout), ._12__GND(1'b0),
    ._11__B1(B1), ._10__A1(A9), ._9__S1(S9));
  _7483 u_7483_2 (
    ._1__A4(A8), ._2__S3(S7), ._3__A3(A7), ._4__B3(B7), ._5__Vcc(1'b1), ._6__S2(S6), ._7__B2(B6),
    ._8__A2(A6), ._16__B4(B8), ._15__S4(S8), ._14_Cout(n7483_2__14_cout), ._13__Cin(n7483_3__14_cout),
    ._12__GND(1'b0), ._11__B1(B5), ._10__A1(A5), ._9__S1(S5));
  _7483 u_7483_3 (
    ._1__A4(A4), ._2__S3(S3), ._3__A3(A3), ._4__B3(B3_2), ._5__Vcc(1'b1), ._6__S2(S2), ._7__B2(B2_2),
    ._8__A2(A2), ._16__B4(B4_2), ._15__S4(S4), ._14_Cout(n7483_3__14_cout), ._13__Cin(Cin), ._12__GND(1'b0),
    ._11__B1(B1_2), ._10__A1(A1), ._9__S1(S1));
endmodule

module _2_s__complementer_12_bit (
  input  E12,
  input  E11,
  input  E10,
  input  E9,
  input  E8,
  input  E7,
  input  E6,
  input  E5,
  input  E4,
  input  E3,
  input  E2,
  input  E1,
  output C,
  output E12_2,
  output E11_2,
  output E10_2,
  output E09,
  output E08,
  output E07,
  output E06,
  output E05,
  output E04,
  output E03,
  output E02,
  output E01
);

  wire n7404_1__2__1y, n7404_1__4__2y, n7404_1__6__3y, n7404_1__8__4y, n7404_1__10__5y, n7404_1__12__6y,
       n7404_2__2__1y, n7404_2__4__2y, n7404_2__6__3y, n7404_2__8__4y, n7404_2__10__5y, n7404_2__12__6y;

  _7404 u_7404_1 (
    ._1__1A(E12), ._2__1Y(n7404_1__2__1y), ._3__2A(E11), ._4__2Y(n7404_1__4__2y), ._5__3A(E10),
    ._6__3Y(n7404_1__6__3y), ._7__GND(1'b0), ._14__Vcc(1'b1), ._13__6A(E9), ._12__6Y(n7404_1__12__6y),
    ._11__5A(E8), ._10__5Y(n7404_1__10__5y), ._9__4A(E7), ._8__4Y(n7404_1__8__4y));
  _12_bit_add_1_or_0 u_12_bit_add_1_or_0_1 (
    .OV(1'b1), .A12(n7404_1__2__1y), .A11(n7404_1__4__2y), .A10(n7404_1__6__3y), .A9(n7404_1__12__6y),
    .A8(n7404_1__10__5y), .A7(n7404_1__8__4y), .A6(n7404_2__2__1y), .A5(n7404_2__4__2y), .A4(n7404_2__6__3y),
    .A3(n7404_2__12__6y), .A2(n7404_2__10__5y), .A1(n7404_2__8__4y), .E12(E12_2), .E11(E11_2), .E10(E10_2),
    .E09(E09), .E08(E08), .E07(E07), .E06(E06), .E05(E05), .E04(E04), .E03(E03), .E02(E02), .E01(E01), .C(C));
  _7404 u_7404_2 (
    ._1__1A(E6), ._2__1Y(n7404_2__2__1y), ._3__2A(E5), ._4__2Y(n7404_2__4__2y), ._5__3A(E4),
    ._6__3Y(n7404_2__6__3y), ._7__GND(1'b0), ._14__Vcc(1'b1), ._13__6A(E3), ._12__6Y(n7404_2__12__6y),
    ._11__5A(E2), ._10__5Y(n7404_2__10__5y), ._9__4A(E1), ._8__4Y(n7404_2__8__4y));
endmodule

module _12_bit__1_bit_AND (
  input  A12,
  input  A11,
  input  A10,
  input  A9,
  input  A8,
  input  A7,
  input  A6,
  input  A5,
  input  A4,
  input  A3,
  input  A2,
  input  A1,
  input  B,
  output E12,
  output E11,
  output E10,
  output E09,
  output E08,
  output E07,
  output E06,
  output E05,
  output E04,
  output E03,
  output E02,
  output E01
);

  _7408 u_7408_1 (
    ._1__1A(A12), ._2__1B(B), ._3__1Y(E12), ._4__2A(A11), ._5__2B(B), ._6__2Y(E11), ._7__GND(1'b0),
    ._14__Vcc(1'b1), ._13__4B(A10), ._12__4A(B), ._11__4Y(E10), ._10__3B(A9), ._9__3A(B), ._8__3Y(E09));
  _7408 u_7408_2 (
    ._1__1A(A8), ._2__1B(B), ._3__1Y(E08), ._4__2A(A7), ._5__2B(B), ._6__2Y(E07), ._7__GND(1'b0),
    ._14__Vcc(1'b1), ._13__4B(A6), ._12__4A(B), ._11__4Y(E06), ._10__3B(A5), ._9__3A(B), ._8__3Y(E05));
  _7408 u_7408_3 (
    ._1__1A(A4), ._2__1B(B), ._3__1Y(E04), ._4__2A(A3), ._5__2B(B), ._6__2Y(E03), ._7__GND(1'b0),
    ._14__Vcc(1'b1), ._13__4B(A2), ._12__4A(B), ._11__4Y(E02), ._10__3B(A1), ._9__3A(B), ._8__3Y(E01));
endmodule

module Sticky_OR (
  input  B31,
  input  B30,
  input  B29,
  input  B28,
  input  B27,
  input  B26,
  input  B25,
  input  B24,
  input  B23,
  input  B22,
  input  B21,
  input  B19,
  output S,
  output S___R,
  output S_R_MSB
);

  wire n7432_1__3__1y, n7432_1__6__2y, n7432_1__8__3y, n7432_1__11__4y, n7432_2__3__1y, n7432_2__6__2y,
       n7432_2__8__3y, n7432_2__11__4y;

  _7432 u_7432_1 (
    ._1__1A(B31), ._2__1B(B30), ._3__1Y(n7432_1__3__1y), ._4__2A(n7432_1__3__1y), ._5__2B(B29),
    ._6__2Y(n7432_1__6__2y), ._7__GND(1'b0), ._14__Vcc(1'b1), ._13__4B(B27), ._12__4A(n7432_1__8__3y),
    ._11__4Y(n7432_1__11__4y), ._10__3B(B28), ._9__3A(n7432_1__6__2y), ._8__3Y(n7432_1__8__3y));
  _7432 u_7432_2 (
    ._1__1A(n7432_1__11__4y), ._2__1B(B26), ._3__1Y(n7432_2__3__1y), ._4__2A(n7432_2__3__1y), ._5__2B(B25),
    ._6__2Y(n7432_2__6__2y), ._7__GND(1'b0), ._14__Vcc(1'b1), ._13__4B(B23), ._12__4A(n7432_2__8__3y),
    ._11__4Y(n7432_2__11__4y), ._10__3B(B24), ._9__3A(n7432_2__6__2y), ._8__3Y(n7432_2__8__3y));
  _7432 u_7432_3 (
    ._1__1A(n7432_2__11__4y), ._2__1B(B22), ._3__1Y(S), ._4__2A(S), ._5__2B(B21), ._6__2Y(S___R),
    ._7__GND(1'b0), ._14__Vcc(1'b1), ._13__4B(B19), ._12__4A(S___R), ._11__4Y(S_R_MSB));  // open: _10__3B, _9__3A, _8__3Y
endmodule

module Rounder (
  input  [31:0] in_1,
  input  in_2,
  input  in_3,
  input  [11:0] in_4,
  output out_5,
  output Carry,
  output Integer,
  output M0,
  output M1,
  output M2,
  output M3,
  output M4,
  output M5,
  output M6,
  output [11:0] out_15,
  output M7,
  output M8,
  output M9,
  output M10,
  output M11,
  output M12,
  output M13,
  output M14,
  output M15,
  output M16,
  output M17,
  output M18
);

  wire n4_bit_add_1_or_0_2_cout, n12_bit_add_1_or_0_1_c, n7408_1__3__1y, sticky_or_1_s_r_msb;

  _4_bit_add_1_or_0 u_4_bit_add_1_or_0_1 (
    .A4(in_1[31]), .A3(in_1[30]), .A2(in_1[29]), .A1(in_1[28]), .Cout(Carry), .S4(Integer), .S3(M0), .S2(M1),
    .S1(M2), .Cin(n4_bit_add_1_or_0_2_cout));
  _4_bit_add_1_or_0 u_4_bit_add_1_or_0_2 (
    .A4(in_1[27]), .A3(in_1[26]), .A2(in_1[25]), .A1(in_1[24]), .Cout(n4_bit_add_1_or_0_2_cout), .S4(M3),
    .S3(M4), .S2(M5), .S1(M6), .Cin(n12_bit_add_1_or_0_1_c));
  _12_bit_add_1_or_0 u_12_bit_add_1_or_0_1 (
    .OV(n7408_1__3__1y), .A12(in_1[23]), .A11(in_1[22]), .A10(in_1[21]), .A9(in_1[20]), .A8(in_1[19]),
    .A7(in_1[18]), .A6(in_1[17]), .A5(in_1[16]), .A4(in_1[15]), .A3(in_1[14]), .A2(in_1[13]), .A1(in_1[12]),
    .E12(M7), .E11(M8), .E10(M9), .E09(M10), .E08(M11), .E07(M12), .E06(M13), .E05(M14), .E04(M15),
    .E03(M16), .E02(M17), .E01(M18), .C(n12_bit_add_1_or_0_1_c));
  Sticky_OR sticky_or_1 (
    .B31(in_1[0]), .B30(in_1[1]), .B29(in_1[2]), .B28(in_1[3]), .B27(in_1[4]), .B26(in_1[5]), .B25(in_1[6]),
    .B24(in_1[7]), .B23(in_1[8]), .B22(in_1[9]), .B21(in_1[10]), .B19(in_1[12]), .S_R_MSB(sticky_or_1_s_r_msb));  // open: S, S___R
  _7408 u_7408_1 (
    ._1__1A(sticky_or_1_s_r_msb), ._2__1B(in_1[11]), ._3__1Y(n7408_1__3__1y), ._4__2A(in_2), ._5__2B(in_3),
    ._6__2Y(out_5));  // open: _7__GND, _14__Vcc, _13__4B, _12__4A, _11__4Y, _10__3B, _9__3A, _8__3Y
  _12_bit_add_1_or_0 u_12_bit_add_1_or_0_2 (
    .OV(Carry), .A12(in_4[11]), .A11(in_4[10]), .A10(in_4[9]), .A9(in_4[8]), .A8(in_4[7]), .A7(in_4[6]),
    .A6(in_4[5]), .A5(in_4[4]), .A4(in_4[3]), .A3(in_4[2]), .A2(in_4[1]), .A1(in_4[0]), .E12(out_15[11]),
    .E11(out_15[10]), .E10(out_15[9]), .E09(out_15[8]), .E08(out_15[7]), .E07(out_15[6]), .E06(out_15[5]),
    .E05(out_15[4]), .E04(out_15[3]), .E03(out_15[2]), .E02(out_15[1]), .E01(out_15[0]));  // open: C
endmodule
