// Logisim project OFFLINE_3_DRAFT_5.circ as structural Verilog: 25 circuits, main circuit main
module main (
);

  SUBTRACTOR subtractor_1 ();  // open: A4, A3, A2, A1, B4, B3, B2, B1, Cout, S4, S3, S2, S1
  OR or_1 ();  // open: A4, A3, A2, A1, B4, B3, B2, B1, S4, S3, S2, S1
  ADDER adder_1 ();  // open: A4, A3, A2, A1, B4, B3, B2, B1, Cout, S4, S3, S2, S1
  NOR nor_1 ();  // open: A4, A3, A2, A1, B4, B3, B2, B1, S4, S3, S2, S1
  SRL srl_1 ();  // open: A4, A3, A2, A1, SB4, SB3, SB2, SB1, S4, S3, S2, S1
  SLL sll_1 ();  // open: A4, A3, A2, A1, SB4, SB3, SB2, SB1, S4, S3, S2, S1
  AND and_1 ();  // open: A4, A3, A2, A1, B4, B3, B2, B1, S4, S3, S2, S1

  // Notes on the sheet:
  //   0000
  //   1100
  //   0110
  //   1110
  //   1101
  //   1110
  //   1111
endmodule

module ADDER (
  input  A4,
  input  A3,
  input  A2,
  input  A1,
  input  B4,
  input  B3,
  input  B2,
  input  B1,
  output Cout,
  output S4,
  output S3,
  output S2,
  output S1
);

  _7483 u_7483_1 (
    ._1__A4(A4), ._2__S3(S3), ._3__A3(A3), ._4__B3(B3), ._5__Vcc(1'b1), ._6__S2(S2), ._7__B2(B2),
    ._8__A2(A2), ._16__B4(B4), ._15__S4(S4), ._14_Cout(Cout), ._13__Cin(1'b0), ._12__GND(1'b0), ._11__B1(B1),
    ._10__A1(A1), ._9__S1(S1));
endmodule

module SUBTRACTOR (
  input  A4,
  input  A3,
  input  A2,
  input  A1,
  input  B4,
  input  B3,
  input  B2,
  input  B1,
  output Cout,
  output S4,
  output S3,
  output S2,
  output S1
);

  wire n7404_1__2__1y, n7404_1__4__2y, n7404_1__6__3y, n7404_1__8__4y;

  _7483 u_7483_1 (
    ._1__A4(A4), ._2__S3(S3), ._3__A3(A3), ._4__B3(n7404_1__2__1y), ._5__Vcc(1'b1), ._6__S2(S2),
    ._7__B2(n7404_1__6__3y), ._8__A2(A2), ._16__B4(n7404_1__4__2y), ._15__S4(S4), ._14_Cout(Cout),
    ._13__Cin(1'b1), ._12__GND(1'b0), ._11__B1(n7404_1__8__4y), ._10__A1(A1), ._9__S1(S1));
  _7404 u_7404_1 (
    ._1__1A(B3), ._2__1Y(n7404_1__2__1y), ._3__2A(B4), ._4__2Y(n7404_1__4__2y), ._5__3A(B2),
    ._6__3Y(n7404_1__6__3y), ._7__GND(1'b0), ._14__Vcc(1'b1), ._9__4A(B1), ._8__4Y(n7404_1__8__4y));  // open: _13__6A, _12__6Y, _11__5A, _10__5Y
endmodule

module NOR (
  input  A4,
  input  A3,
  input  A2,
  input  A1,
  input  B4,
  input  B3,
  input  B2,
  input  B1,
  output S4,
  output S3,
  output S2,
  output S1
);

  _7402 u_7402_1 (
    ._1__1Y(S4), ._2__1A(A4), ._3__1B(B4), ._4__2Y(S3), ._5__2A(A3), ._6__2B(B3), ._7__GND(1'b0),
    ._14__Vcc(1'b1), ._13__4Y(S1), ._12__4B(B1), ._11__4A(A1), ._10__3Y(S2), ._9__3B(B2), ._8__3A(A2));
endmodule

module AND (
  input  A4,
  input  A3,
  input  A2,
  input  A1,
  input  B4,
  input  B3,
  input  B2,
  input  B1,
  output S4,
  output S3,
  output S2,
  output S1
);

  _7408 u_7408_1 (
    ._1__1A(A4), ._2__1B(B4), ._3__1Y(S4), ._4__2A(A3), ._5__2B(B3), ._6__2Y(S3), ._7__GND(1'b0),
    ._14__Vcc(1'b1), ._13__4B(B1), ._12__4A(A1), ._11__4Y(S1), ._10__3B(B2), ._9__3A(A2), ._8__3Y(S2));
endmodule

module OR (
  input  A4,
  input  A3,
  input  A2,
  input  A1,
  input  B4,
  input  B3,
  input  B2,
  input  B1,
  output S4,
  output S3,
  output S2,
  output S1
);

  _7432 u_7432_1 (
    ._1__1A(A4), ._2__1B(B4), ._3__1Y(S4), ._4__2A(A3), ._5__2B(B3), ._6__2Y(S3), ._7__GND(1'b0),
    ._14__Vcc(1'b1), ._13__4B(B1), ._12__4A(A1), ._11__4Y(S1), ._10__3B(B2), ._9__3A(A2), ._8__3Y(S2));
endmodule

module JunkSRL (
  input  A4,
  input  A3,
  input  A2,
  input  A1,
  input  SB4,
  input  SB3,
  input  SB2,
  input  SB1,
  output [3:0] out_9
);

  wire n7432_1__3__1y;
  wire [1:0] n7432_1__11__4y;

  Shifter #(.width(4)) shifter_1 (.in({A4, A3, A2, A1}), .\dist (n7432_1__11__4y), .out(out_9));
  _7432 u_7432_1 (
    ._1__1A(SB4), ._2__1B(SB3), ._3__1Y(n7432_1__3__1y), ._4__2A(n7432_1__3__1y), ._5__2B(SB2),
    ._6__2Y(n7432_1__11__4y[1]), ._7__GND(1'b0), ._14__Vcc(1'b1), ._13__4B(n7432_1__3__1y), ._12__4A(SB1),
    ._11__4Y(n7432_1__11__4y[0]));  // open: _10__3B, _9__3A, _8__3Y
endmodule

module SRL (
  input  A4,
  input  A3,
  input  A2,
  input  A1,
  input  SB4,
  input  SB3,
  input  SB2,
  input  SB1,
  output S4,
  output S3,
  output S2,
  output S1
);

  wire [15:4] shifter_1_out;

  Shifter #(.width(16), .shift("lr")) shifter_1 (
    .in({{12{1'b0}}, A4, A3, A2, A1}), .\dist ({SB4, SB3, SB2, SB1}), .out({shifter_1_out, S4, S3, S2, S1}));
endmodule

module SLL (
  input  A4,
  input  A3,
  input  A2,
  input  A1,
  input  SB4,
  input  SB3,
  input  SB2,
  input  SB1,
  output S4,
  output S3,
  output S2,
  output S1
);

  wire [15:4] shifter_1_out;

  Shifter #(.width(16)) shifter_1 (
    .in({{12{1'b0}}, A4, A3, A2, A1}), .\dist ({SB4, SB3, SB2, SB1}), .out({shifter_1_out, S4, S3, S2, S1}));
endmodule

module EEPROM_TEST (
  input  [15:0] in_1
);

  wire clock_1_out;
  wire [3:0] register_circuit_1_p4, register_circuit_1_p7, register_circuit_1_p8, undriven;
  wire [15:0] rom_1_data;

  RAM #(.addrWidth(4), .dataWidth(4), .bus("asynch")) ram_1 (.addr(undriven));  // open: data, sel, ld, clr
  ROM #(.addrWidth(16), .dataWidth(16)) rom_1 (.addr(in_1), .data(rom_1_data), .sel(1'b1));
  Clock clock_1 (.out(clock_1_out));
  // REGISTER_CIRCUIT register_circuit_1: pin names not known; wires that end beside it: rom_1_data[11:8], rom_1_data[7:4], rom_1_data[7:4], register_circuit_1_p4, clock_1_out, 1'b0, register_circuit_1_p7, register_circuit_1_p8
  NOR nor_1 (
    .A4(register_circuit_1_p7[3]), .A3(register_circuit_1_p7[2]), .A2(register_circuit_1_p7[1]),
    .A1(register_circuit_1_p7[0]), .B4(register_circuit_1_p8[3]), .B3(register_circuit_1_p8[2]),
    .B2(register_circuit_1_p8[1]), .B1(register_circuit_1_p8[0]), .S4(register_circuit_1_p4[3]),
    .S3(register_circuit_1_p4[2]), .S2(register_circuit_1_p4[1]), .S1(register_circuit_1_p4[0]));

  // Notes on the sheet:
  //   contents of rom_1 (hex, n*v repeats v):
  //   2a 14 11 14 44
endmodule

// WRITER
module WRITE_REGISTER_CIRCUIT (
  input  [3:0] WRITE_DATA,
  input  B4,
  input  B3,
  input  B2,
  input  B1,
  input  WRITE_SIGNAL,
  input  CLOCK,
  input  CLEAR,
  output [3:0] READ__zero,
  output [3:0] READ__t0,
  output [3:0] READ__t1,
  output [3:0] READ__t2,
  output [3:0] READ__t3,
  output [3:0] READ__t4,
  output [3:0] READ__sp,
  output [3:0] READ__ra,
  output [3:0] READ__v0,
  output [3:0] READ__v1,
  output [3:0] READ__a0,
  output [3:0] READ__a1,
  output [3:0] READ__s0,
  output [3:0] READ__s1
);

  wire n7408_1__3__1y, n7408_1__6__2y, n7408_1__8__3y, n7408_1__11__4y, n7408_2__3__1y, n7408_2__6__2y,
       n7408_2__8__3y, n7408_3__3__1y, n7408_3__6__2y, n7408_3__11__4y, n7408_4__8__3y, n7408_4__11__4y,
       n74238_1__7__y7, n74238_1__9__y6, n74238_1__10__y5, n74238_1__11__y4, n74238_1__12__y3,
       n74238_1__13__y2, n74238_1__14__y1, n74238_2__10__y5, n74238_2__11__y4, n74238_2__12__y3,
       n74238_2__13__y2, n74238_2__14__y1, n74238_2__15__y0;

  _74238 u_74238_1 (
    ._1__A0(B1), ._2__A1(B2), ._3__A2(B3), ._4__E1_prime(B4), ._5__E2_prime(1'b0), ._6__E3(1'b1),
    ._7__Y7(n74238_1__7__y7), ._8__GND(1'b0), ._16__Vcc(1'b1), ._14__Y1(n74238_1__14__y1),
    ._13__Y2(n74238_1__13__y2), ._12__Y3(n74238_1__12__y3), ._11__Y4(n74238_1__11__y4),
    ._10__Y5(n74238_1__10__y5), ._9__Y6(n74238_1__9__y6));  // open: _15__Y0
  _74238 u_74238_2 (
    ._1__A0(B1), ._2__A1(B2), ._3__A2(B3), ._4__E1_prime(1'b0), ._5__E2_prime(1'b0), ._6__E3(B4),
    ._8__GND(1'b0), ._16__Vcc(1'b1), ._15__Y0(n74238_2__15__y0), ._14__Y1(n74238_2__14__y1),
    ._13__Y2(n74238_2__13__y2), ._12__Y3(n74238_2__12__y3), ._11__Y4(n74238_2__11__y4),
    ._10__Y5(n74238_2__10__y5));  // open: _7__Y7, _9__Y6
  _7408 u_7408_1 (
    ._1__1A(WRITE_SIGNAL), ._2__1B(n74238_1__14__y1), ._3__1Y(n7408_1__3__1y), ._4__2A(n74238_1__12__y3),
    ._5__2B(WRITE_SIGNAL), ._6__2Y(n7408_1__6__2y), ._7__GND(1'b0), ._14__Vcc(1'b1),
    ._13__4B(n74238_1__13__y2), ._12__4A(WRITE_SIGNAL), ._11__4Y(n7408_1__11__4y), ._10__3B(WRITE_SIGNAL),
    ._9__3A(n74238_1__11__y4), ._8__3Y(n7408_1__8__3y));
  _7408 u_7408_2 (
    ._1__1A(WRITE_SIGNAL), ._2__1B(n74238_1__10__y5), ._3__1Y(n7408_2__3__1y), ._4__2A(n74238_1__7__y7),
    ._5__2B(WRITE_SIGNAL), ._6__2Y(n7408_2__6__2y), ._7__GND(1'b0), ._14__Vcc(1'b1),
    ._10__3B(n74238_1__9__y6), ._9__3A(WRITE_SIGNAL), ._8__3Y(n7408_2__8__3y));  // open: _13__4B, _12__4A, _11__4Y
  _7408 u_7408_3 (
    ._1__1A(WRITE_SIGNAL), ._2__1B(n74238_2__15__y0), ._3__1Y(n7408_3__3__1y), ._4__2A(n74238_2__14__y1),
    ._5__2B(WRITE_SIGNAL), ._6__2Y(n7408_3__6__2y), ._7__GND(1'b0), ._14__Vcc(1'b1),
    ._13__4B(n74238_2__13__y2), ._12__4A(WRITE_SIGNAL), ._11__4Y(n7408_3__11__4y),
    ._10__3B(n74238_2__12__y3), ._9__3A(WRITE_SIGNAL));  // open: _8__3Y
  _7408 u_7408_4 (
    ._14__Vcc(1'b1), ._13__4B(n74238_2__11__y4), ._12__4A(WRITE_SIGNAL), ._11__4Y(n7408_4__11__4y),
    ._10__3B(n74238_2__10__y5), ._9__3A(WRITE_SIGNAL), ._8__3Y(n7408_4__8__3y));  // open: _1__1A, _2__1B, _3__1Y, _4__2A, _5__2B, _6__2Y, _7__GND
  Register #(.width(4)) zero (.Q(READ__zero), .clk(CLOCK), .clr(CLEAR));  // open: D, en
  Register #(.width(4)) t0 (.D(WRITE_DATA), .en(n7408_1__3__1y), .Q(READ__t0), .clk(CLOCK), .clr(CLEAR));
  Register #(.width(4)) t1 (.D(WRITE_DATA), .en(n7408_1__11__4y), .Q(READ__t1), .clk(CLOCK), .clr(CLEAR));
  Register #(.width(4)) t2 (.D(WRITE_DATA), .en(n7408_1__6__2y), .Q(READ__t2), .clk(CLOCK), .clr(CLEAR));
  Register #(.width(4)) t3 (.D(WRITE_DATA), .en(n7408_1__8__3y), .Q(READ__t3), .clk(CLOCK), .clr(CLEAR));
  Register #(.width(4)) t4 (.D(WRITE_DATA), .en(n7408_2__3__1y), .Q(READ__t4), .clk(CLOCK), .clr(CLEAR));
  Register #(.width(4)) sp (.D(WRITE_DATA), .en(n7408_2__8__3y), .Q(READ__sp), .clk(CLOCK), .clr(CLEAR));
  Register #(.width(4)) ra (.D(WRITE_DATA), .en(n7408_2__6__2y), .Q(READ__ra), .clk(CLOCK), .clr(CLEAR));
  Register #(.width(4)) v0 (.D(WRITE_DATA), .en(n7408_3__3__1y), .Q(READ__v0), .clk(CLOCK), .clr(CLEAR));
  Register #(.width(4)) v1 (.D(WRITE_DATA), .en(n7408_3__6__2y), .Q(READ__v1), .clk(CLOCK), .clr(CLEAR));
  Register #(.width(4)) a0 (.D(WRITE_DATA), .en(n7408_3__11__4y), .Q(READ__a0), .clk(CLOCK), .clr(CLEAR));
  Register #(.width(4)) a1 (.D(WRITE_DATA), .en(n74238_2__12__y3), .Q(READ__a1), .clk(CLOCK), .clr(CLEAR));
  Register #(.width(4)) s0 (.D(WRITE_DATA), .en(n7408_4__11__4y), .Q(READ__s0), .clk(CLOCK), .clr(CLEAR));
  Register #(.width(4)) register_1 (.D(WRITE_DATA), .en(n7408_4__8__3y), .Q(READ__s1), .clk(CLOCK), .clr(CLEAR));
endmodule

// READ_SELECTOR
module READ_SELECTER (
  input  B4,
  input  B3,
  input  B2,
  input  B1,
  input  s1,
  input  zero,
  input  s0,
  input  t0,
  input  a1,
  input  t1,
  input  a0,
  input  t2,
  input  v1,
  input  t3,
  input  v0,
  input  t4,
  input  ra,
  input  sp,
  output S
);

  wire n7404_1__2__1y, n74151_1__5__y, n74151_2__5__y;

  _74151 u_74151_1 (
    ._1__D3(t2), ._2__D2(t1), ._3__D1(t0), ._4__D0(zero), ._5__Y(n74151_1__5__y), ._7__nG(B4),
    ._8__GND(1'b0), ._16__Vcc(1'b1), ._15__D4(t3), ._14__D5(t4), ._13__D6(sp), ._12__D7(ra), ._11__A(B1),
    ._10__B(B2), ._9__C(B3));  // open: _6__W
  _7404 u_7404_1 (
    ._1__1A(B4), ._2__1Y(n7404_1__2__1y), ._7__GND(1'b0), ._14__Vcc(1'b1));  // open: _3__2A, _4__2Y, _5__3A, _6__3Y, _13__6A, _12__6Y, _11__5A, _10__5Y, _9__4A, _8__4Y
  _74151 u_74151_2 (
    ._1__D3(a1), ._2__D2(a0), ._3__D1(v1), ._4__D0(v0), ._5__Y(n74151_2__5__y), ._7__nG(n7404_1__2__1y),
    ._8__GND(1'b0), ._16__Vcc(1'b1), ._15__D4(s0), ._14__D5(s1), ._11__A(B1), ._10__B(B2), ._9__C(B3));  // open: _6__W, _13__D6, _12__D7
  _74157 u_74157_1 (
    ._1__S(B4), ._2__A1(n74151_1__5__y), ._3__B1(n74151_2__5__y), ._4__Y1(S), ._16__Vcc(1'b1), ._15__G(1'b0));  // open: _5__A2, _6__B2, _7__Y2, _8__GND, _14__A4, _13__B4, _12__Y4, _11__A3, _10__B3, _9__Y3
endmodule

// READER
module READ_REGISTER_CIRCUIT (
  input  B4,
  input  B3,
  input  B2,
  input  B1,
  input  [3:0] zero,
  input  [3:0] t0,
  input  [3:0] t1,
  input  [3:0] t2,
  input  [3:0] t3,
  input  [3:0] t4,
  input  [3:0] sp,
  input  [3:0] ra,
  input  [3:0] v0,
  input  [3:0] v1,
  input  [3:0] a0,
  input  [3:0] a1,
  input  [3:0] s0,
  input  [3:0] s1,
  output R4,
  output R3,
  output R2,
  output R1
);

  READ_SELECTER read_selecter_1 (
    .B4(B4), .B3(B3), .B2(B2), .B1(B1), .zero(zero[3]), .t0(t0[3]), .t1(t1[3]), .t2(t2[3]), .t3(t3[3]),
    .t4(t4[3]), .sp(sp[3]), .S(R4), .s1(s1[3]), .s0(s0[3]), .a1(a1[3]), .a0(a0[3]), .v1(v1[3]), .v0(v0[3]),
    .ra(ra[3]));
  READ_SELECTER read_selecter_2 (
    .B4(B4), .B3(B3), .B2(B2), .B1(B1), .zero(zero[2]), .t0(t0[2]), .t1(t1[2]), .t2(t2[2]), .t3(t3[2]),
    .t4(t4[2]), .sp(sp[2]), .S(R3), .s1(s1[2]), .s0(s0[2]), .a1(a1[2]), .a0(a0[2]), .v1(v1[2]), .v0(v0[2]),
    .ra(ra[2]));
  READ_SELECTER read_selecter_3 (
    .B4(B4), .B3(B3), .B2(B2), .B1(B1), .zero(zero[1]), .t0(t0[1]), .t1(t1[1]), .t2(t2[1]), .t3(t3[1]),
    .t4(t4[1]), .sp(sp[1]), .S(R2), .s1(s1[1]), .s0(s0[1]), .a1(a1[1]), .a0(a0[1]), .v1(v1[1]), .v0(v0[1]),
    .ra(ra[1]));
  READ_SELECTER read_selecter_4 (
    .B4(B4), .B3(B3), .B2(B2), .B1(B1), .zero(zero[0]), .t0(t0[0]), .t1(t1[0]), .t2(t2[0]), .t3(t3[0]),
    .t4(t4[0]), .sp(sp[0]), .S(R1), .s1(s1[0]), .s0(s0[0]), .a1(a1[0]), .a0(a0[0]), .v1(v1[0]), .v0(v0[0]),
    .ra(ra[0]));
endmodule

module REGISTER_CIRCUIT (
  input  [3:0] READ_REGISTER_1,
  input  [3:0] READ_REGISTER_2,
  input  [3:0] WRITE_REGISTER,
  input  CLK,
  input  [3:0] WRITE_DATA,
  input  WRITE_SIGNAL,
  input  CLR,
  output [3:0] out_8,
  output [3:0] out_9,
  output [3:0] out_10,
  output [3:0] out_11,
  output [3:0] out_12,
  output [3:0] out_13,
  output [3:0] out_14,
  output [3:0] out_15,
  output [3:0] READ_DATA_1,
  output [3:0] READ_DATA_2
);

  wire [3:0] write_register_circuit_1_read__a0, write_register_circuit_1_read__a1,
       write_register_circuit_1_read__s0, write_register_circuit_1_read__s1,
       write_register_circuit_1_read__v0, write_register_circuit_1_read__v1;

  WRITE_REGISTER_CIRCUIT write_register_circuit_1 (
    .WRITE_DATA(WRITE_DATA), .B4(WRITE_REGISTER[3]), .B3(WRITE_REGISTER[2]), .B2(WRITE_REGISTER[1]),
    .B1(WRITE_REGISTER[0]), .WRITE_SIGNAL(WRITE_SIGNAL), .CLOCK(CLK), .CLEAR(CLR), .READ__zero(out_8),
    .READ__t0(out_9), .READ__t1(out_10), .READ__t2(out_11), .READ__t3(out_12), .READ__t4(out_13),
    .READ__sp(out_14), .READ__ra(out_15), .READ__v0(write_register_circuit_1_read__v0),
    .READ__v1(write_register_circuit_1_read__v1), .READ__a0(write_register_circuit_1_read__a0),
    .READ__a1(write_register_circuit_1_read__a1), .READ__s0(write_register_circuit_1_read__s0),
    .READ__s1(write_register_circuit_1_read__s1));
  READ_REGISTER_CIRCUIT read_register_circuit_1 (
    .B4(READ_REGISTER_1[3]), .B3(READ_REGISTER_1[2]), .B2(READ_REGISTER_1[1]), .B1(READ_REGISTER_1[0]),
    .zero(out_8), .t0(out_9), .t1(out_10), .t2(out_11), .t3(out_12), .t4(out_13), .sp(out_14), .ra(out_15),
    .v0(write_register_circuit_1_read__v0), .v1(write_register_circuit_1_read__v1),
    .a0(write_register_circuit_1_read__a0), .a1(write_register_circuit_1_read__a1),
    .s0(write_register_circuit_1_read__s0), .s1(write_register_circuit_1_read__s1), .R4(READ_DATA_1[3]),
    .R3(READ_DATA_1[2]), .R2(READ_DATA_1[1]), .R1(READ_DATA_1[0]));
  READ_REGISTER_CIRCUIT read_register_circuit_2 (
    .B4(READ_REGISTER_2[3]), .B3(READ_REGISTER_2[2]), .B2(READ_REGISTER_2[1]), .B1(READ_REGISTER_2[0]),
    .zero(out_8), .t0(out_9), .t1(out_10), .t2(out_11), .t3(out_12), .t4(out_13), .sp(out_14), .ra(out_15),
    .v0(write_register_circuit_1_read__v0), .v1(write_register_circuit_1_read__v1),
    .a0(write_register_circuit_1_read__a0), .a1(write_register_circuit_1_read__a1),
    .s0(write_register_circuit_1_read__s0), .s1(write_register_circuit_1_read__s1), .R4(READ_DATA_2[3]),
    .R3(READ_DATA_2[2]), .R2(READ_DATA_2[1]), .R1(READ_DATA_2[0]));
endmodule

module EEPROM_CON (
  input  [15:0] in_1
);

  wire clock_1_out, register_circuit_1_p4;
  wire [3:0] register_circuit_1_p7, register_circuit_1_p8;
  wire [15:0] rom_1_data;

  INSTRUCTION_MEMORY instruction_memory_1 ();  // open: ADDRESS, DATA
  CONTROL control_1 ();  // open: OpCode, ALUOp, RegDst, Jump, Branch_Equal, MemToReg, MemRead, MemWrite, ALUSrc, RegWrite, Branch_Not_Equal
  ROM #(.addrWidth(16), .dataWidth(16)) rom_1 (.addr(in_1), .data(rom_1_data), .sel(1'b1));
  ALU alu_1 ();  // open: R1, R2, OP, Y3, Y2, Y1, Y0, ZERO, NOT_ZERO
  Clock clock_1 (.out(clock_1_out));
  // REGISTER_CIRCUIT register_circuit_1: pin names not known; wires that end beside it: rom_1_data[11:8], rom_1_data[7:4], rom_1_data[7:4], register_circuit_1_p4, clock_1_out, 1'b0, register_circuit_1_p7, register_circuit_1_p8, register_circuit_1_p7[3], register_circuit_1_p7[2], register_circuit_1_p7[1]

  // Notes on the sheet:
  //   contents of rom_1 (hex, n*v repeats v):
  //   1414 6311 9414 b444 4000
endmodule

module ALU (
  input  [3:0] R1,
  input  [3:0] R2,
  input  [3:0] OP,
  output Y3,
  output NOT_ZERO,
  output ZERO,
  output Y2,
  output Y1,
  output Y0
);

  wire adder_1_s1, adder_1_s2, adder_1_s3, adder_1_s4, and_1_s1, and_1_s2, and_1_s3, and_1_s4,
       n7432_1__3__1y, n7432_1__6__2y, n7432_1__8__3y, n7432_1__11__4y, n7432_2__3__1y, n7432_2__6__2y,
       n7432_2__8__3y, n7432_2__11__4y, n7432_3__3__1y, n7432_3__6__2y, n7432_3__11__4y, n7432_4__3__1y,
       n7432_4__6__2y, n74238_1__7__y7, n74238_1__9__y6, n74238_1__10__y5, n74238_1__12__y3,
       n74238_1__13__y2, n74238_1__14__y1, n74238_1__15__y0, n74238_2__7__y7, n74238_2__9__y6,
       n74238_2__10__y5, n74238_2__11__y4, n74238_2__12__y3, n74238_2__13__y2, n74238_2__14__y1,
       n74238_2__15__y0, nor_1_s1, nor_1_s2, nor_1_s3, nor_1_s4, or_1_s1, or_1_s2, or_1_s3, or_1_s4,
       sll_1_s1, sll_1_s2, sll_1_s3, sll_1_s4, srl_1_s1, srl_1_s2, srl_1_s3, srl_1_s4, subtractor_1_s1,
       subtractor_1_s2, subtractor_1_s3, subtractor_1_s4, undriven, undriven_2, undriven_3, undriven_4;

  ADDER adder_1 (
    .A4(R1[3]), .A3(R1[2]), .A2(R1[1]), .A1(R1[0]), .B4(R2[3]), .B3(R2[2]), .B2(R2[1]), .B1(R2[0]),
    .S4(adder_1_s4), .S3(adder_1_s3), .S2(adder_1_s2), .S1(adder_1_s1));  // open: Cout
  OR or_1 (
    .A4(R1[3]), .A3(R1[2]), .A2(R1[1]), .A1(R1[0]), .B4(R2[3]), .B3(R2[2]), .B2(R2[1]), .B1(R2[0]),
    .S4(or_1_s4), .S3(or_1_s3), .S2(or_1_s2), .S1(or_1_s1));
  AND and_1 (
    .A4(R1[3]), .A3(R1[2]), .A2(R1[1]), .A1(R1[0]), .B4(R2[3]), .B3(R2[2]), .B2(R2[1]), .B1(R2[0]),
    .S4(and_1_s4), .S3(and_1_s3), .S2(and_1_s2), .S1(and_1_s1));
  _74238 u_74238_1 (
    ._1__A0(OP[0]), ._2__A1(OP[1]), ._3__A2(OP[2]), ._4__E1_prime(OP[3]), ._5__E2_prime(OP[3]),
    ._6__E3(1'b1), ._7__Y7(n74238_1__7__y7), ._8__GND(1'b0), ._16__Vcc(1'b1), ._15__Y0(n74238_1__15__y0),
    ._14__Y1(n74238_1__14__y1), ._13__Y2(n74238_1__13__y2), ._12__Y3(n74238_1__12__y3),
    ._10__Y5(n74238_1__10__y5), ._9__Y6(n74238_1__9__y6));  // open: _11__Y4
  _74238 u_74238_2 (
    ._1__A0(OP[0]), ._2__A1(OP[1]), ._3__A2(OP[2]), ._4__E1_prime(1'b0), ._5__E2_prime(1'b0), ._6__E3(OP[3]),
    ._7__Y7(n74238_2__7__y7), ._8__GND(1'b0), ._16__Vcc(1'b1), ._15__Y0(n74238_2__15__y0),
    ._14__Y1(n74238_2__14__y1), ._13__Y2(n74238_2__13__y2), ._12__Y3(n74238_2__12__y3),
    ._11__Y4(n74238_2__11__y4), ._10__Y5(n74238_2__10__y5), ._9__Y6(n74238_2__9__y6));
  _7432 u_7432_1 (
    ._1__1A(n74238_1__9__y6), ._2__1B(n74238_2__12__y3), ._3__1Y(n7432_1__3__1y), ._4__2A(n74238_1__15__y0),
    ._5__2B(n74238_1__7__y7), ._6__2Y(n7432_1__6__2y), ._7__GND(1'b0), ._14__Vcc(1'b1),
    ._13__4B(n74238_1__10__y5), ._12__4A(n74238_2__11__y4), ._11__4Y(n7432_1__11__4y),
    ._10__3B(n74238_2__15__y0), ._9__3A(n74238_2__7__y7), ._8__3Y(n7432_1__8__3y));
  _7432 u_7432_2 (
    ._1__1A(n74238_1__14__y1), ._2__1B(n7432_1__3__1y), ._3__1Y(n7432_2__3__1y), ._4__2A(n7432_2__3__1y),
    ._5__2B(n74238_2__14__y1), ._6__2Y(n7432_2__6__2y), ._7__GND(1'b0), ._13__4B(n7432_1__6__2y),
    ._12__4A(n74238_1__13__y2), ._11__4Y(n7432_2__11__4y), ._10__3B(n7432_2__11__4y),
    ._9__3A(n74238_1__12__y3), ._8__3Y(n7432_2__8__3y));  // open: _14__Vcc
  NOR nor_1 (
    .A4(R1[3]), .A3(R1[2]), .A2(R1[1]), .A1(R1[0]), .B4(R2[3]), .B3(R2[2]), .B2(R2[1]), .B1(R2[0]),
    .S4(nor_1_s4), .S3(nor_1_s3), .S2(nor_1_s2), .S1(nor_1_s1));
  SUBTRACTOR subtractor_1 (
    .A4(R1[3]), .A3(R1[2]), .A2(R1[1]), .A1(R1[0]), .B4(R2[3]), .B3(R2[2]), .B2(R2[1]), .B1(R2[0]),
    .S4(subtractor_1_s4), .S3(subtractor_1_s3), .S2(subtractor_1_s2), .S1(subtractor_1_s1));  // open: Cout
  _74148 u_74148_1 (
    ._1__I4(n74238_2__13__y2), ._2__I5(n74238_2__10__y5), ._3__I6(n74238_2__9__y6), ._5__nEI__NC(1'b0),
    ._6__A2(undriven_2), ._7__A1(undriven), ._8__GND(1'b0), ._16__Vcc(1'b1), ._14__nGS__NC(undriven_4),
    ._13__I3(n7432_1__11__4y), ._12__I2(n7432_1__8__3y), ._11__I1(n7432_2__8__3y), ._10__I0(n7432_2__6__2y),
    ._9__A0(undriven_3));  // open: _4__I7, _15__nEO__NC
  SRL srl_1 (
    .A4(R1[3]), .A3(R1[2]), .A2(R1[1]), .A1(R1[0]), .SB4(R2[3]), .SB3(R2[2]), .SB2(R2[1]), .SB1(R2[0]),
    .S4(srl_1_s4), .S3(srl_1_s3), .S2(srl_1_s2), .S1(srl_1_s1));
  SLL sll_1 (
    .A4(R1[3]), .A3(R1[2]), .A2(R1[1]), .A1(R1[0]), .SB4(R2[3]), .SB3(R2[2]), .SB2(R2[1]), .SB1(R2[0]),
    .S4(sll_1_s4), .S3(sll_1_s3), .S2(sll_1_s2), .S1(sll_1_s1));
  _7432 u_7432_3 (
    ._1__1A(undriven_2), ._2__1B(undriven_4), ._3__1Y(n7432_3__3__1y), ._4__2A(undriven_4),
    ._5__2B(undriven), ._6__2Y(n7432_3__6__2y), ._7__GND(1'b0), ._13__4B(undriven_4), ._12__4A(undriven_3),
    ._11__4Y(n7432_3__11__4y));  // open: _14__Vcc, _10__3B, _9__3A, _8__3Y
  _74151 u_74151_1 (
    ._1__D3(or_1_s4), ._2__D2(and_1_s4), ._3__D1(subtractor_1_s4), ._4__D0(adder_1_s4), ._5__Y(Y3),
    ._7__nG(1'b0), ._8__GND(1'b0), ._16__Vcc(1'b1), ._15__D4(nor_1_s4), ._14__D5(srl_1_s4),
    ._13__D6(sll_1_s4), ._12__D7(R1[3]), ._11__A(n7432_3__11__4y), ._10__B(n7432_3__6__2y),
    ._9__C(n7432_3__3__1y));  // open: _6__W
  _74151 u_74151_2 (
    ._1__D3(or_1_s3), ._2__D2(and_1_s3), ._3__D1(subtractor_1_s3), ._4__D0(adder_1_s3), ._5__Y(Y2),
    ._7__nG(1'b0), ._8__GND(1'b0), ._16__Vcc(1'b1), ._15__D4(nor_1_s3), ._14__D5(srl_1_s3),
    ._13__D6(sll_1_s3), ._12__D7(R1[2]), ._11__A(n7432_3__11__4y), ._10__B(n7432_3__6__2y),
    ._9__C(n7432_3__3__1y));  // open: _6__W
  _74151 u_74151_3 (
    ._1__D3(or_1_s2), ._2__D2(and_1_s2), ._3__D1(subtractor_1_s2), ._4__D0(adder_1_s2), ._5__Y(Y1),
    ._7__nG(1'b0), ._8__GND(1'b0), ._16__Vcc(1'b1), ._15__D4(nor_1_s2), ._14__D5(srl_1_s2),
    ._13__D6(sll_1_s2), ._12__D7(R1[1]), ._11__A(n7432_3__11__4y), ._10__B(n7432_3__6__2y),
    ._9__C(n7432_3__3__1y));  // open: _6__W
  _74151 u_74151_4 (
    ._1__D3(or_1_s1), ._2__D2(and_1_s1), ._3__D1(subtractor_1_s1), ._4__D0(adder_1_s1), ._5__Y(Y0),
    ._7__nG(1'b0), ._8__GND(1'b0), ._16__Vcc(1'b1), ._15__D4(nor_1_s1), ._14__D5(srl_1_s1),
    ._13__D6(sll_1_s1), ._12__D7(R1[0]), ._11__A(n7432_3__11__4y), ._10__B(n7432_3__6__2y),
    ._9__C(n7432_3__3__1y));  // open: _6__W
  _7432 u_7432_4 (
    ._1__1A(Y3), ._2__1B(Y2), ._3__1Y(n7432_4__3__1y), ._4__2A(n7432_4__3__1y), ._5__2B(Y1),
    ._6__2Y(n7432_4__6__2y), ._7__GND(n7432_3__3__1y), ._14__Vcc(1'b1), ._13__4B(n7432_4__6__2y),
    ._12__4A(Y0), ._11__4Y(NOT_ZERO));  // open: _10__3B, _9__3A, _8__3Y
  _7404 u_7404_1 (
    ._1__1A(NOT_ZERO), ._2__1Y(ZERO), ._14__Vcc(1'b1));  // open: _3__2A, _4__2Y, _5__3A, _6__3Y, _7__GND, _13__6A, _12__6Y, _11__5A, _10__5Y, _9__4A, _8__4Y

  // Notes on the sheet:
  //   SUB 0
  //   LW 1
  //   BNEQ 2
  //   BEQ 3
  //   J 4
  //   ORI 5
  //   ADD 6
  //   SUBI 7
  //   ANDI 8
  //   SW 9
  //   NOR A
  //   ADDI B
  //   OR C
  //   SRL D
  //   SLL E
  //   AND F
endmodule

module CONTROLJunk (
  input  [3:0] OpCode,
  output Branch,
  output Jump,
  output MemWrite,
  output MemRead
);

  wire n7404_1__2__1y, n7404_1__4__2y, n7404_1__6__3y, n7404_1__12__6y, n7408_1__3__1y, n7408_1__8__3y,
       n7408_1__11__4y, n7408_3__3__1y, n7408_3__6__2y;

  _7408 u_7408_1 (
    ._1__1A(n7404_1__12__6y), ._2__1B(n7404_1__2__1y), ._3__1Y(n7408_1__3__1y), ._4__2A(n7408_1__3__1y),
    ._5__2B(OpCode[1]), ._6__2Y(Branch), ._7__GND(1'b0), ._14__Vcc(1'b1), ._13__4B(n7404_1__12__6y),
    ._12__4A(n7404_1__4__2y), ._11__4Y(n7408_1__11__4y), ._10__3B(n7408_1__11__4y), ._9__3A(n7404_1__6__3y),
    ._8__3Y(n7408_1__8__3y));
  _7408 u_7408_2 (
    ._1__1A(n7408_1__8__3y), ._2__1B(OpCode[2]), ._3__1Y(Jump));  // open: _4__2A, _5__2B, _6__2Y, _7__GND, _14__Vcc, _13__4B, _12__4A, _11__4Y, _10__3B, _9__3A, _8__3Y
  _7408 u_7408_3 (
    ._1__1A(n7404_1__2__1y), ._2__1B(n7404_1__4__2y), ._3__1Y(n7408_3__3__1y), ._4__2A(n7408_3__3__1y),
    ._5__2B(OpCode[0]), ._6__2Y(n7408_3__6__2y), ._7__GND(1'b0), ._13__4B(OpCode[3]),
    ._12__4A(n7408_3__6__2y), ._11__4Y(MemWrite), ._10__3B(n7404_1__12__6y), ._9__3A(n7408_3__6__2y),
    ._8__3Y(MemRead));  // open: _14__Vcc
  _7404 u_7404_1 (
    ._1__1A(OpCode[2]), ._2__1Y(n7404_1__2__1y), ._3__2A(OpCode[1]), ._4__2Y(n7404_1__4__2y),
    ._5__3A(OpCode[0]), ._6__3Y(n7404_1__6__3y), ._7__GND(1'b0), ._14__Vcc(1'b1), ._13__6A(OpCode[3]),
    ._12__6Y(n7404_1__12__6y));  // open: _11__5A, _10__5Y, _9__4A, _8__4Y
endmodule

module CONTROL (
  input  [3:0] OpCode,
  output [3:0] ALUOp,
  output RegDst,
  output Jump,
  output Branch_Equal,
  output Branch_Not_Equal,
  output MemToReg,
  output MemRead,
  output MemWrite,
  output ALUSrc,
  output RegWrite
);

  wire n7432_1__3__1y, n7432_1__6__2y, n7432_1__11__4y, n7432_2__3__1y, n7432_3__3__1y, n7432_3__6__2y,
       n7432_3__8__3y, n7432_3__11__4y, n74238_1__9__y6, n74238_1__15__y0, n74238_2__7__y7, n74238_2__11__y4,
       n74238_2__13__y2;

  _74238 u_74238_1 (
    ._1__A0(OpCode[0]), ._2__A1(OpCode[1]), ._3__A2(OpCode[2]), ._4__E1_prime(OpCode[3]),
    ._5__E2_prime(OpCode[3]), ._6__E3(1'b1), ._8__GND(1'b0), ._16__Vcc(1'b1), ._15__Y0(n74238_1__15__y0),
    ._14__Y1(MemRead), ._13__Y2(Branch_Not_Equal), ._12__Y3(Branch_Equal), ._11__Y4(Jump),
    ._9__Y6(n74238_1__9__y6));  // open: _7__Y7, _10__Y5
  _74238 u_74238_2 (
    ._1__A0(OpCode[0]), ._2__A1(OpCode[1]), ._3__A2(OpCode[2]), ._4__E1_prime(1'b0), ._5__E2_prime(1'b0),
    ._6__E3(OpCode[3]), ._7__Y7(n74238_2__7__y7), ._8__GND(1'b0), ._16__Vcc(1'b1), ._14__Y1(MemWrite),
    ._13__Y2(n74238_2__13__y2), ._11__Y4(n74238_2__11__y4));  // open: _15__Y0, _12__Y3, _10__Y5, _9__Y6
  _7432 u_7432_1 (
    ._1__1A(Branch_Equal), ._2__1B(Branch_Not_Equal), ._3__1Y(n7432_1__3__1y), ._4__2A(n7432_1__3__1y),
    ._5__2B(Jump), ._6__2Y(n7432_1__6__2y), ._7__GND(1'b0), ._14__Vcc(1'b1), ._13__4B(n7432_1__6__2y),
    ._12__4A(MemWrite), ._11__4Y(n7432_1__11__4y));  // open: _10__3B, _9__3A, _8__3Y
  _7432 u_7432_2 (
    ._1__1A(n74238_2__13__y2), ._2__1B(n7432_3__11__4y), ._3__1Y(n7432_2__3__1y), ._4__2A(n7432_2__3__1y),
    ._5__2B(n74238_2__11__y4), ._6__2Y(RegDst), ._7__GND(1'b0), ._14__Vcc(1'b1));  // open: _13__4B, _12__4A, _11__4Y, _10__3B, _9__3A, _8__3Y
  _7432 u_7432_3 (
    ._1__1A(Branch_Not_Equal), ._2__1B(Branch_Equal), ._3__1Y(n7432_3__3__1y), ._4__2A(n74238_1__9__y6),
    ._5__2B(n7432_3__3__1y), ._6__2Y(n7432_3__6__2y), ._7__GND(1'b0), ._14__Vcc(1'b1),
    ._13__4B(n7432_3__8__3y), ._12__4A(n74238_2__7__y7), ._11__4Y(n7432_3__11__4y),
    ._10__3B(n74238_1__15__y0), ._9__3A(n7432_3__6__2y), ._8__3Y(n7432_3__8__3y));
  _7404 u_7404_1 (
    ._1__1A(RegDst), ._2__1Y(ALUSrc), ._3__2A(n7432_1__11__4y), ._4__2Y(RegWrite), ._7__GND(1'b0),
    ._14__Vcc(1'b1));  // open: _5__3A, _6__3Y, _13__6A, _12__6Y, _11__5A, _10__5Y, _9__4A, _8__4Y

  assign ALUOp = OpCode;
  assign MemToReg = MemRead;

  // Notes on the sheet:
  //   SUB 0
  //   LW 1
  //   BNEQ 2
  //   BEQ 3
  //   J 4
  //   ORI 5
  //   ADD 6
  //   SUBI 7
  //   ANDI 8
  //   SW 9
  //   NOR A
  //   ADDI B
  //   OR C
  //   SRL D
  //   SLL E
  //   AND F
endmodule

module INSTRUCTION_MEMORY (
  input  [7:0] ADDRESS,
  output [15:0] DATA
);

  ROM #(.dataWidth(16)) rom_1 (.addr(ADDRESS), .data(DATA), .sel(1'b1));

  // Notes on the sheet:
  //   contents of rom_1 (hex, n*v repeats v):
  //   b023 7032 b334 6231 234 a135 9323 d331 343a 4170 e441 1334 b66e 9621 9630 c131 8531 5225 1631 f352
  //   4170 2311
endmodule

module DATAPATH (
  input  in_1,
  output [7:0] out_2,
  output [3:0] t0,
  output [3:0] t1,
  output [3:0] t2,
  output [3:0] t3,
  output [3:0] t4,
  output [3:0] zero,
  output [3:0] sp,
  output [3:0] ra
);

  wire alu_1_not_zero, alu_1_zero, clock_1_out, control_1_alusrc, control_1_branch_equal,
       control_1_branch_not_equal, control_1_jump, control_1_memread, control_1_memtoreg, control_1_memwrite,
       control_1_regdst, control_1_regwrite, jal_control_1_regwrite, jr_1_jr, n7408_1__3__1y, n7408_1__6__2y,
       n7432_1__3__1y, n7432_2__3__1y;
  wire [3:0] alu_1_y0, control_1_aluop, data_memory_1_data_bus, instruction_memory_1_data,
       instruction_memory_1_data_2, instruction_memory_1_data_3, instruction_memory_1_data_4,
       jal_control_1_write__ra, jr_1_ra_2, mux_1_out_4, mux_2_out_4, mux_4_out_4, mux_5_out_4, mux_6_out_4,
       mux_7_out_4, mux_8_out_4, mux_9_out_4, mux_10_out_4, mux_11_out_4, mux_12_out_4, mux_13_out_4,
       n8_bit_adder_1_sum, n8_bit_adder_1_sum_2, register_circuit_1_read_data_1,
       register_circuit_1_read_data_2;
  wire [7:0] n8_bit_adder_2_sum, n7486_1__11__4y;

  Clock clock_1 (.out(clock_1_out));
  Register register_1 (.D({mux_12_out_4, mux_13_out_4}), .Q(out_2), .clk(clock_1_out), .clr(in_1));  // open: en
  INSTRUCTION_MEMORY instruction_memory_1 (
    .ADDRESS(out_2),
    .DATA({instruction_memory_1_data_4, instruction_memory_1_data_3, instruction_memory_1_data_2, instruction_memory_1_data}));
  MUX mux_1 (.Select(jr_1_jr), .Zero_Select(instruction_memory_1_data_3), .One_Select(jr_1_ra_2), .out_4(mux_1_out_4));
  _8_BIT_ADDER u_8_bit_adder_1 (.A(out_2), .B(8'h1), .SUM({n8_bit_adder_1_sum_2, n8_bit_adder_1_sum}));
  CONTROL control_1 (
    .OpCode(instruction_memory_1_data_4), .ALUOp(control_1_aluop), .RegDst(control_1_regdst),
    .Jump(control_1_jump), .Branch_Equal(control_1_branch_equal), .MemToReg(control_1_memtoreg),
    .MemRead(control_1_memread), .MemWrite(control_1_memwrite), .ALUSrc(control_1_alusrc),
    .RegWrite(control_1_regwrite), .Branch_Not_Equal(control_1_branch_not_equal));
  MUX mux_2 (
    .Select(control_1_regdst), .Zero_Select(instruction_memory_1_data_2),
    .One_Select(instruction_memory_1_data), .out_4(mux_2_out_4));
  MUX mux_3 (
    .Select(instruction_memory_1_data[3]), .Zero_Select(4'b0000), .One_Select(4'b1111),
    .out_4(n7486_1__11__4y[7:4]));
  MUX mux_4 (.Select(jal_control_1_regwrite), .Zero_Select(mux_2_out_4), .One_Select(4'b0111), .out_4(mux_4_out_4));
  JAL_CONTROL jal_control_1 (
    .JUMP(control_1_jump), .Addr(instruction_memory_1_data), .REGWRITE(jal_control_1_regwrite),
    .WRITE__ra(jal_control_1_write__ra));
  _7486 u_7486_1 (
    ._1__1A(instruction_memory_1_data[2]), ._2__1B(instruction_memory_1_data[3]),
    ._3__1Y(n7486_1__11__4y[2]), ._4__2A(instruction_memory_1_data[3]),
    ._5__2B(instruction_memory_1_data[1]), ._6__2Y(n7486_1__11__4y[1]), ._7__GND(1'b0), ._14__Vcc(1'b1),
    ._13__4B(instruction_memory_1_data[0]), ._12__4A(instruction_memory_1_data[3]),
    ._11__4Y(n7486_1__11__4y[0]));  // open: _10__3B, _9__3A, _8__3Y
  _7408 u_7408_1 (
    ._1__1A(control_1_branch_equal), ._2__1B(alu_1_zero), ._3__1Y(n7408_1__3__1y),
    ._4__2A(control_1_branch_not_equal), ._5__2B(alu_1_not_zero), ._6__2Y(n7408_1__6__2y), ._7__GND(1'b0),
    ._14__Vcc(1'b1));  // open: _13__4B, _12__4A, _11__4Y, _10__3B, _9__3A, _8__3Y
  MUX mux_5 (
    .Select(jal_control_1_regwrite), .Zero_Select(mux_11_out_4), .One_Select(jal_control_1_write__ra),
    .out_4(mux_5_out_4));
  _7432 u_7432_1 (
    ._1__1A(control_1_regwrite), ._2__1B(jal_control_1_regwrite), ._3__1Y(n7432_1__3__1y));  // open: _4__2A, _5__2B, _6__2Y, _7__GND, _14__Vcc, _13__4B, _12__4A, _11__4Y, _10__3B, _9__3A, _8__3Y
  REGISTER_CIRCUIT register_circuit_1 (
    .READ_REGISTER_1(mux_1_out_4), .READ_REGISTER_2(instruction_memory_1_data_2),
    .WRITE_REGISTER(mux_4_out_4), .WRITE_DATA(mux_5_out_4), .WRITE_SIGNAL(n7432_1__3__1y), .CLK(clock_1_out),
    .CLR(in_1), .READ_DATA_1(register_circuit_1_read_data_1), .READ_DATA_2(register_circuit_1_read_data_2),
    .out_8(zero), .out_9(t0), .out_10(t1), .out_11(t2), .out_12(t3), .out_13(t4), .out_14(sp), .out_15(ra));
  MUX mux_6 (
    .Select(control_1_alusrc), .Zero_Select(register_circuit_1_read_data_2),
    .One_Select(instruction_memory_1_data), .out_4(mux_6_out_4));
  JR jr_1 (
    .opcode(instruction_memory_1_data_4), .input1(instruction_memory_1_data_3),
    .input2(instruction_memory_1_data_2), .ra(instruction_memory_1_data), .JR(jr_1_jr), .ra_2(jr_1_ra_2));
  _8_BIT_ADDER u_8_bit_adder_2 (
    .A({mux_12_out_4, mux_13_out_4}), .B({n7486_1__11__4y[7:4], 1'b0, n7486_1__11__4y[2:0]}),
    .SUM(n8_bit_adder_2_sum));
  _7432 u_7432_2 (
    ._1__1A(n7408_1__6__2y), ._2__1B(n7408_1__3__1y), ._3__1Y(n7432_2__3__1y), ._7__GND(1'b0), ._14__Vcc(1'b1));  // open: _4__2A, _5__2B, _6__2Y, _13__4B, _12__4A, _11__4Y, _10__3B, _9__3A, _8__3Y
  MUX mux_7 (
    .Select(n7432_2__3__1y), .Zero_Select(n8_bit_adder_1_sum_2), .One_Select(n8_bit_adder_2_sum[7:4]),
    .out_4(mux_7_out_4));
  ALU alu_1 (
    .R1(register_circuit_1_read_data_1), .R2(mux_6_out_4), .OP(control_1_aluop), .Y3(alu_1_y0[3]),
    .Y2(alu_1_y0[2]), .Y1(alu_1_y0[1]), .Y0(alu_1_y0[0]), .ZERO(alu_1_zero), .NOT_ZERO(alu_1_not_zero));
  MUX mux_8 (
    .Select(n7432_2__3__1y), .Zero_Select(n8_bit_adder_1_sum), .One_Select(n8_bit_adder_2_sum[3:0]),
    .out_4(mux_8_out_4));
  MUX mux_9 (
    .Select(control_1_jump), .Zero_Select(mux_7_out_4), .One_Select(instruction_memory_1_data_3),
    .out_4(mux_9_out_4));
  MUX mux_10 (
    .Select(control_1_jump), .Zero_Select(mux_8_out_4), .One_Select(instruction_memory_1_data_2),
    .out_4(mux_10_out_4));
  DATA_MEMORY data_memory_1 (
    .Address_bus(alu_1_y0), .in_4(register_circuit_1_read_data_2), .CLK(clock_1_out), .CLR(in_1),
    .Data_bus(data_memory_1_data_bus), .MemWrite(control_1_memread), .in_2(control_1_memwrite));
  MUX mux_11 (
    .Select(control_1_memtoreg), .Zero_Select(alu_1_y0), .One_Select(data_memory_1_data_bus),
    .out_4(mux_11_out_4));
  MUX mux_12 (.Select(jr_1_jr), .Zero_Select(mux_9_out_4), .One_Select(4'b0000), .out_4(mux_12_out_4));
  MUX mux_13 (
    .Select(jr_1_jr), .Zero_Select(mux_10_out_4), .One_Select(register_circuit_1_read_data_1),
    .out_4(mux_13_out_4));
endmodule

module MUX (
  input  Select,
  input  [3:0] Zero_Select,
  input  [3:0] One_Select,
  output [3:0] out_4
);

  _74157 u_74157_1 (
    ._1__S(Select), ._2__A1(Zero_Select[3]), ._3__B1(One_Select[3]), ._4__Y1(out_4[3]),
    ._5__A2(Zero_Select[2]), ._6__B2(One_Select[2]), ._7__Y2(out_4[2]), ._8__GND(1'b0), ._16__Vcc(1'b1),
    ._15__G(1'b0), ._14__A4(Zero_Select[1]), ._13__B4(One_Select[1]), ._12__Y4(out_4[1]),
    ._11__A3(Zero_Select[0]), ._10__B3(One_Select[0]), ._9__Y3(out_4[0]));
endmodule

module DATA_MEMORY (
  input  MemWrite,
  input  in_2,
  input  [3:0] Address_bus,
  input  [3:0] in_4,
  input  CLK,
  input  CLR,
  output [3:0] Data_bus
);

  RAM #(.addrWidth(4), .dataWidth(4), .bus("separate")) ram_1 (
    .addr(Address_bus), .din(in_4), .data(Data_bus), .str(in_2), .clk(CLK), .ld(MemWrite), .clr(CLR));  // open: sel

  // Notes on the sheet:
  //   Data bus
  //   MemRead
endmodule

module _8_BIT_ADDER (
  input  [7:0] A,
  input  [7:0] B,
  output [7:0] SUM
);

  wire adder_1_s1, adder_1_s2, adder_1_s3, adder_1_s4, adder_3_cout;

  ADDER adder_1 (
    .A4(A[7]), .A3(A[6]), .A2(A[5]), .A1(A[4]), .B4(B[7]), .B3(B[6]), .B2(B[5]), .B1(B[4]), .S4(adder_1_s4),
    .S3(adder_1_s3), .S2(adder_1_s2), .S1(adder_1_s1));  // open: Cout
  ADDER adder_2 (
    .A4(adder_1_s4), .A3(adder_1_s3), .A2(adder_1_s2), .A1(adder_1_s1), .B4(1'b0), .B3(1'b0), .B2(1'b0),
    .B1(adder_3_cout), .S4(SUM[7]), .S3(SUM[6]), .S2(SUM[5]), .S1(SUM[4]));  // open: Cout
  ADDER adder_3 (
    .A4(A[3]), .A3(A[2]), .A2(A[1]), .A1(A[0]), .B4(B[3]), .B3(B[2]), .B2(B[1]), .B1(B[0]),
    .Cout(adder_3_cout), .S4(SUM[3]), .S3(SUM[2]), .S2(SUM[1]), .S1(SUM[0]));
endmodule

module JAL_CONTROL (
  input  JUMP,
  input  [3:0] Addr,
  output REGWRITE,
  output [3:0] WRITE__ra
);

  wire n7432_1__3__1y, n7432_1__6__2y, n7432_1__11__4y;

  _7432 u_7432_1 (
    ._1__1A(Addr[3]), ._2__1B(Addr[2]), ._3__1Y(n7432_1__3__1y), ._4__2A(n7432_1__3__1y), ._5__2B(Addr[1]),
    ._6__2Y(n7432_1__6__2y), ._7__GND(1'b0), ._14__Vcc(1'b1), ._13__4B(n7432_1__6__2y), ._12__4A(Addr[0]),
    ._11__4Y(n7432_1__11__4y));  // open: _10__3B, _9__3A, _8__3Y
  _7408 u_7408_1 (
    ._1__1A(JUMP), ._2__1B(n7432_1__11__4y), ._3__1Y(REGWRITE), ._7__GND(1'b0), ._14__Vcc(1'b1));  // open: _4__2A, _5__2B, _6__2Y, _13__4B, _12__4A, _11__4Y, _10__3B, _9__3A, _8__3Y

  assign WRITE__ra = Addr;
endmodule

module JR (
  input  [3:0] opcode,
  input  [3:0] input1,
  input  [3:0] input2,
  input  [3:0] ra,
  output JR,
  output [3:0] ra_2
);

  wire n7408_1__3__1y, n7408_1__6__2y, n7408_1__8__3y, n7408_2__3__1y, n7408_2__6__2y, n7408_2__8__3y,
       n7408_2__11__4y, n7408_3__3__1y, n7408_3__6__2y, n7408_3__11__4y;

  _7408 u_7408_1 (
    ._1__1A(opcode[3]), ._2__1B(opcode[2]), ._3__1Y(n7408_1__3__1y), ._4__2A(n7408_1__3__1y),
    ._5__2B(opcode[1]), ._6__2Y(n7408_1__6__2y), ._7__GND(1'b0), ._14__Vcc(1'b1), ._10__3B(n7408_1__6__2y),
    ._9__3A(opcode[0]), ._8__3Y(n7408_1__8__3y));  // open: _13__4B, _12__4A, _11__4Y
  _7408 u_7408_2 (
    ._1__1A(n7408_1__8__3y), ._2__1B(input1[0]), ._3__1Y(n7408_2__3__1y), ._4__2A(n7408_2__3__1y),
    ._5__2B(input1[3]), ._6__2Y(n7408_2__6__2y), ._7__GND(1'b0), ._14__Vcc(1'b1), ._13__4B(n7408_2__8__3y),
    ._12__4A(input1[1]), ._11__4Y(n7408_2__11__4y), ._10__3B(n7408_2__6__2y), ._9__3A(input1[2]),
    ._8__3Y(n7408_2__8__3y));
  _7408 u_7408_3 (
    ._1__1A(n7408_2__11__4y), ._2__1B(input2[3]), ._3__1Y(n7408_3__3__1y), ._4__2A(n7408_3__3__1y),
    ._5__2B(input2[2]), ._6__2Y(n7408_3__6__2y), ._7__GND(1'b0), ._14__Vcc(1'b1), ._13__4B(n7408_3__6__2y),
    ._12__4A(input2[1]), ._11__4Y(n7408_3__11__4y), ._10__3B(n7408_3__11__4y), ._9__3A(input2[0]), ._8__3Y(JR));

  assign ra_2 = ra;
endmodule
